// Logisim project Project.circ as structural Verilog: 26 circuits, main circuit main
module main (
  output negative,
  output zero,
  output overflow,
  output signed_overflow
);

  wire alu_1_a_0, alu_1_a_1, alu_1_a_2, alu_1_a_3, and_1_out, and_2_out, and_3_out, and_4_out, and_5_out,
       and_6_out, Aout_R, AR_MR_W, clock_1_out, command, d_register_1_out_0, d_register_1_out_1,
       d_register_1_out_2, d_register_1_out_3, D_W, DR_R, DR_W, IR_0, IR_1, IR_2, IR_3, IR_R, IR_to_MBR,
       IR_W, L_R_W, led_1_1_out1, led_1_1_out2, led_1_1_out3, led_1_1_out4, led_1_1_out5, led_1_1_out6,
       led_1_1_out7, led_1_1_out_4_2, led_1_1_out_7_2, MAR_R, MAR_W, MBR_R, MBR_W, mode, my_buffer_1_out_2,
       my_buffer_2_out_2, my_buffer_3_out_2, my_buffer_4_out_2, my_buffer_5_out_2, my_buffer_6_out_2,
       my_buffer_7_out_2, my_buffer_8_out_2, my_buffer_9_out_2, not_1_out, not_2_out, or_1_out, or_2_out,
       or_3_out, or_4_out, or_5_out, or_6_out, or_7_out, or_8_out, or_9_out, or_10_out, or_11_out, or_12_out,
       or_13_out, or_14_out, or_15_out, or_16_out, or_17_out, or_18_out, or_19_out, or_20_out, or_21_out,
       pc_1_out_0, pc_1_out_1, pc_1_out_2, pc_1_out_3, PC_inc, PC_R, r0_0, r0_1, r0_2, r0_3, R0_R,
       r0_register_1_out_0, r0_register_1_out_1, r0_register_1_out_2, r0_register_1_out_3, R0_W,
       ram_4bit_1_out0, ram_4bit_1_out1, ram_4bit_1_out2, ram_4bit_1_out3, ram_4bit_1_r0_0, ram_4bit_1_r0_1,
       ram_4bit_1_r0_2, ram_4bit_1_r0_3, RAM_to_DR, re_to_Aout, REG_12_R, REG_12_W, Reg_to_RAM,
       register_4_bit_1_out_0, register_4_bit_1_out_1, register_4_bit_1_out_2, register_4_bit_2_out_0,
       register_4_bit_2_out_1, register_4_bit_2_out_2, register_4_bit_2_out_3, register_4_bit_3_out_0,
       register_4_bit_3_out_1, register_4_bit_3_out_2, register_4_bit_3_out_3;

  Clock clock_1 (.out(clock_1_out));
  and and_1 (and_1_out, ~PC_R, IR_0);  // AND_Gate
  CU cu_1 (
    .clock(clock_1_out), .In3(IR_3), .In2(IR_2), .In1(IR_1), .In0(IR_0), .mode(mode), .MAR_R(MAR_R),
    .AR_MR_W(AR_MR_W), .IR_to_MBR(IR_to_MBR), .R0_R(R0_R), .MBR_R(MBR_R), .L_R_W(L_R_W),
    .RAM_to_DR(RAM_to_DR), .DR_W(DR_W), .re_to_Aout(re_to_Aout), .command(command), .REG_12_R(REG_12_R),
    .PC_R(PC_R), .MAR_W(MAR_W), .DR_R(DR_R), .MBR_W(MBR_W), .IR_W(IR_W), .PC_inc(PC_inc), .IR_R(IR_R),
    .Reg_to_RAM(Reg_to_RAM), .R0_W(R0_W), .Aout_R(Aout_R), .REG_12_W(REG_12_W), .D_W(D_W));
  PC pc_1 (
    .increase_en(PC_inc), .Read_en(PC_R), .Out_3(pc_1_out_3), .Out_2(pc_1_out_2), .Out_1(pc_1_out_1),
    .Out_0(pc_1_out_0));
  or or_1 (or_1_out, pc_1_out_0, and_1_out);
  my_buffer my_buffer_1 (.out_2(my_buffer_1_out_2), .in_1(MAR_W));
  my_buffer my_buffer_2 (.out_2(my_buffer_2_out_2), .in_1(REG_12_W));
  or or_2 (or_2_out, IR_to_MBR, REG_12_R);
  Register_4_bit register_4_bit_1 (
    .Write_en(my_buffer_1_out_2), .in_0(or_1_out), .in_1(pc_1_out_1), .in_2(pc_1_out_2), .in_3(pc_1_out_3),
    .Read_en(MAR_R), .out_0(register_4_bit_1_out_0), .out_1(register_4_bit_1_out_1),
    .out_2(register_4_bit_1_out_2));  // open: out_3
  not not_1 (not_1_out, IR_1);
  my_buffer my_buffer_3 (.out_2(my_buffer_3_out_2), .in_1(R0_W));
  and and_2 (and_2_out, not_1_out, my_buffer_2_out_2);
  not not_2 (not_2_out, IR_1);
  my_buffer my_buffer_4 (.out_2(my_buffer_4_out_2), .in_1(L_R_W));
  and and_3 (and_3_out, my_buffer_2_out_2, IR_1);
  and and_4 (and_4_out, not_2_out, or_2_out);
  and and_5 (and_5_out, or_2_out, IR_1);
  or or_3 (or_3_out, MBR_W, IR_to_MBR);
  or or_4 (or_4_out, my_buffer_3_out_2, and_2_out);
  my_buffer my_buffer_5 (.out_2(my_buffer_5_out_2), .in_1(DR_W));
  my_buffer my_buffer_6 (.out_2(my_buffer_6_out_2), .in_1(AR_MR_W));
  my_buffer my_buffer_7 (.out_2(my_buffer_7_out_2), .in_1(or_3_out));
  and and_6 (and_6_out, MBR_R, ~REG_12_R);  // AND_Gate
  RAM_4bit ram_4bit_1 (
    .d3(or_8_out), .d2(or_15_out), .d1(or_16_out), .d0(or_20_out), .Write_to_AR_MR(my_buffer_6_out_2),
    .Write_to_Din(my_buffer_5_out_2), .Reg_to_Ram(Reg_to_RAM), .Write_Ram_to_Dout(RAM_to_DR),
    .Read_Dout(DR_R), .Mode(mode), .a2(register_4_bit_1_out_2), .a1(register_4_bit_1_out_1),
    .a0(register_4_bit_1_out_0), .R0_3(ram_4bit_1_r0_3), .R0_2(ram_4bit_1_r0_2), .R0_1(ram_4bit_1_r0_1),
    .R0_0(ram_4bit_1_r0_0), .out3(ram_4bit_1_out3), .out2(ram_4bit_1_out2), .out1(ram_4bit_1_out1),
    .out0(ram_4bit_1_out0));
  Register_4_bit register_4_bit_2 (
    .Write_en(my_buffer_7_out_2), .in_0(or_20_out), .in_1(or_16_out), .in_2(or_15_out), .in_3(or_8_out),
    .Read_en(and_6_out), .out_0(register_4_bit_2_out_0), .out_1(register_4_bit_2_out_1),
    .out_2(register_4_bit_2_out_2), .out_3(register_4_bit_2_out_3));
  R0_Register r0_register_1 (
    .Write_en(or_4_out), .in_0(or_20_out), .in_1(or_16_out), .in_2(or_15_out), .in_3(or_8_out),
    .Read_en(and_4_out), .R0_R_en(R0_R), .out_0(r0_register_1_out_0), .out_1(r0_register_1_out_1),
    .out_2(r0_register_1_out_2), .out_3(r0_register_1_out_3), .read_0(r0_0), .read_1(r0_1), .read_2(r0_2),
    .read_3(r0_3));
  Register_4_bit register_4_bit_3 (
    .Write_en(and_3_out), .in_0(or_20_out), .in_1(or_16_out), .in_2(or_15_out), .in_3(or_8_out),
    .Read_en(and_5_out), .out_0(register_4_bit_3_out_0), .out_1(register_4_bit_3_out_1),
    .out_2(register_4_bit_3_out_2), .out_3(register_4_bit_3_out_3));
  ALU alu_1 (
    .L_3(r0_3), .L_2(r0_2), .L_1(r0_1), .L_0(r0_0), .R_3(or_8_out), .R_2(or_15_out), .R_1(or_16_out),
    .R_0(or_20_out), .Write_to_L_R_Reg(my_buffer_4_out_2), .Reg_to_adder_to_Aout(re_to_Aout),
    .Read_Aout_SR(Aout_R), .Add_Sub_command(command), .negative(negative), .zero(zero), .overflow(overflow),
    .signed_overflow(signed_overflow), .a_3(alu_1_a_3), .a_2(alu_1_a_2), .a_1(alu_1_a_1), .a_0(alu_1_a_0));
  or or_5 (or_5_out, register_4_bit_2_out_3, ram_4bit_1_out3);
  or or_6 (or_6_out, r0_register_1_out_3, or_5_out);
  or or_7 (or_7_out, register_4_bit_3_out_3, or_6_out);
  or or_8 (or_8_out, alu_1_a_3, or_7_out);
  or or_9 (or_9_out, register_4_bit_2_out_2, ram_4bit_1_out2);
  or or_10 (or_10_out, register_4_bit_2_out_1, ram_4bit_1_out1);
  or or_11 (or_11_out, r0_register_1_out_2, or_9_out);
  or or_12 (or_12_out, r0_register_1_out_1, or_10_out);
  or or_13 (or_13_out, register_4_bit_3_out_2, or_11_out);
  or or_14 (or_14_out, register_4_bit_3_out_1, or_12_out);
  or or_15 (or_15_out, alu_1_a_2, or_13_out);
  or or_16 (or_16_out, alu_1_a_1, or_14_out);
  or or_17 (or_17_out, register_4_bit_2_out_0, ram_4bit_1_out0);
  or or_18 (or_18_out, r0_register_1_out_0, or_17_out);
  or or_19 (or_19_out, register_4_bit_3_out_0, or_18_out);
  or or_20 (or_20_out, alu_1_a_0, or_19_out);
  or or_21 (or_21_out, PC_R, D_W);
  my_buffer my_buffer_8 (.out_2(my_buffer_8_out_2), .in_1(or_21_out));
  my_buffer my_buffer_9 (.out_2(my_buffer_9_out_2), .in_1(IR_W));
  D_Register d_register_1 (
    .Write_en(my_buffer_8_out_2), .in_3(ram_4bit_1_r0_3), .in_2(ram_4bit_1_r0_2), .in_1(ram_4bit_1_r0_1),
    .in_0(ram_4bit_1_r0_0), .out_3(d_register_1_out_3), .out_2(d_register_1_out_2),
    .out_1(d_register_1_out_1), .out_0(d_register_1_out_0));
  IR u_ir_1 (
    .d_0(IR_0), .d_1(IR_1), .d_2(IR_2), .d_3(IR_3), .Write_en(my_buffer_9_out_2),
    .in_0(register_4_bit_2_out_0), .in_1(register_4_bit_2_out_1), .in_2(register_4_bit_2_out_2),
    .in_3(register_4_bit_2_out_3), .Read_en(IR_R));  // open: out_0, out_1, out_2, out_3
  LED_1 led_1_1 (
    .In0(d_register_1_out_0), .In1(d_register_1_out_1), .In2(d_register_1_out_2), .In3(d_register_1_out_3),
    .Out1(led_1_1_out1), .Out2(led_1_1_out2), .Out3(led_1_1_out3), .Out4(led_1_1_out4), .Out5(led_1_1_out5),
    .Out6(led_1_1_out6), .Out7(led_1_1_out7), .Out_4_2(led_1_1_out_4_2), .Out_7_2(led_1_1_out_7_2));
  _7_Segment_Display u_7_segment_display_1 (.b(led_1_1_out_4_2), .c(led_1_1_out_7_2));  // open: g, f, a, e, d, dp
  _7_Segment_Display u_7_segment_display_2 (
    .g(led_1_1_out1), .f(led_1_1_out2), .a(led_1_1_out3), .b(led_1_1_out4), .e(led_1_1_out5),
    .d(led_1_1_out6), .c(led_1_1_out7));  // open: dp

  // Notes on the sheet:
  //   Jiahang Wang 261011319
  //   Clock of the CPU
  //   CU
  //   PC
  //   MAR
  //   0
  //   CPU
  //   MBR
  //   R0
  //   R1
  //   ALU
  //   RAM
  //   U Bus
  //   D Register
  //   IR
  //   LED display
endmodule

module Register_4_bit (
  input  Write_en,
  input  in_0,
  input  in_1,
  input  in_2,
  input  in_3,
  input  Read_en,
  output out_0,
  output out_1,
  output out_2,
  output out_3
);

  wire and_1_out, and_2_out, and_3_out, and_4_out, buffer_1_out, buffer_2_out, store_0_q, store_1_q,
       store_2_q, store_3_q;

  and and_1 (and_1_out, in_0, Write_en);
  and and_2 (and_2_out, in_1, Write_en);
  and and_3 (and_3_out, in_2, Write_en);
  and and_4 (and_4_out, in_3, Write_en);
  buf buffer_1 (buffer_1_out, Write_en);
  buf buffer_2 (buffer_2_out, buffer_1_out);
  D_Flip_Flop store_0 (.D(and_1_out), .clk(buffer_2_out), .Q(store_0_q));  // open: Qn, preset, reset
  D_Flip_Flop store_1 (.D(and_2_out), .clk(buffer_2_out), .Q(store_1_q));  // open: Qn, preset, reset
  D_Flip_Flop store_2 (.D(and_3_out), .clk(buffer_2_out), .Q(store_2_q));  // open: Qn, preset, reset
  D_Flip_Flop store_3 (.D(and_4_out), .clk(buffer_2_out), .Q(store_3_q));  // open: Qn, preset, reset
  // Probe on store_3_q
  // Probe on store_2_q
  // Probe on store_1_q
  // Probe on store_0_q
  and and_5 (out_0, store_0_q, Read_en);
  and and_6 (out_1, store_1_q, Read_en);
  and and_7 (out_2, store_2_q, Read_en);
  and and_8 (out_3, store_3_q, Read_en);

  // Notes on the sheet:
  //   current stored 4-bit data
endmodule

module IR (
  input  Write_en,
  input  in_0,
  input  in_1,
  input  in_2,
  input  in_3,
  input  Read_en,
  output out_0,
  output out_1,
  output out_2,
  output out_3,
  output d_0,
  output d_1,
  output d_2,
  output d_3
);

  wire and_1_out, and_2_out, and_3_out, and_4_out, buffer_1_out, buffer_2_out;

  and and_1 (and_1_out, in_0, Write_en);
  and and_2 (and_2_out, in_1, Write_en);
  and and_3 (and_3_out, in_2, Write_en);
  and and_4 (and_4_out, in_3, Write_en);
  buf buffer_1 (buffer_1_out, Write_en);
  buf buffer_2 (buffer_2_out, buffer_1_out);
  D_Flip_Flop store_0 (.D(and_1_out), .clk(buffer_2_out), .Q(d_0));  // open: Qn, preset, reset
  D_Flip_Flop store_1 (.D(and_2_out), .clk(buffer_2_out), .Q(d_1));  // open: Qn, preset, reset
  D_Flip_Flop store_2 (.D(and_3_out), .clk(buffer_2_out), .Q(d_2));  // open: Qn, preset, reset
  D_Flip_Flop store_3 (.D(and_4_out), .clk(buffer_2_out), .Q(d_3));  // open: Qn, preset, reset
  // Probe on d_2
  // Probe on d_3
  // Probe on d_1
  // Probe on d_0
  and and_5 (out_0, d_0, Read_en);
  and and_6 (out_1, d_1, Read_en);
  and and_7 (out_2, d_2, Read_en);
  and and_8 (out_3, d_3, Read_en);
endmodule

module Nibble (
  input  Write_en,
  input  in_0,
  input  in_1,
  input  in_2,
  input  in_3,
  output out_0,
  output out_1,
  output out_2,
  output out_3
);

  wire and_1_out, and_2_out, and_3_out, and_4_out, buffer_1_out, buffer_2_out;

  and and_1 (and_1_out, in_0, Write_en);
  and and_2 (and_2_out, in_1, Write_en);
  and and_3 (and_3_out, in_2, Write_en);
  and and_4 (and_4_out, in_3, Write_en);
  buf buffer_1 (buffer_1_out, Write_en);
  buf buffer_2 (buffer_2_out, buffer_1_out);
  D_Flip_Flop store_bit_0 (.D(and_1_out), .clk(buffer_2_out), .Q(out_0));  // open: Qn, preset, reset
  D_Flip_Flop store_bit_1 (.D(and_2_out), .clk(buffer_2_out), .Q(out_1));  // open: Qn, preset, reset
  D_Flip_Flop store_bit_2 (.D(and_3_out), .clk(buffer_2_out), .Q(out_2));  // open: Qn, preset, reset
  D_Flip_Flop store_bit_3 (.D(and_4_out), .clk(buffer_2_out), .Q(out_3));  // open: Qn, preset, reset
  // Probe on out_3
  // Probe on out_1
  // Probe on out_2
  // Probe on out_0

  // Notes on the sheet:
  //   Current 4 bit data stored in this address
endmodule

module mode_register (
  input  Write_en,
  input  in_0,
  input  Read_en,
  output out_0
);

  wire and_1_out, buffer_1_out, buffer_2_out, store_0_q;

  and and_1 (and_1_out, in_0, Write_en);
  buf buffer_1 (buffer_1_out, Write_en);
  buf buffer_2 (buffer_2_out, buffer_1_out);
  D_Flip_Flop store_0 (.D(and_1_out), .clk(buffer_2_out), .Q(store_0_q));  // open: Qn, preset, reset
  // Probe on store_0_q
  and and_2 (out_0, store_0_q, Read_en);
endmodule

module input_register (
  input  Write_en,
  input  in_0,
  input  in_1,
  input  in_2,
  input  in_3,
  input  Read_en,
  output out_0,
  output out_1,
  output out_2,
  output out_3
);

  wire and_1_out, and_2_out, and_3_out, and_4_out, buffer_1_out, buffer_2_out, store_0_q, store_1_q,
       store_2_q, store_3_q;

  and and_1 (and_1_out, in_0, Write_en);
  and and_2 (and_2_out, in_1, Write_en);
  and and_3 (and_3_out, in_2, Write_en);
  and and_4 (and_4_out, in_3, Write_en);
  buf buffer_1 (buffer_1_out, Write_en);
  buf buffer_2 (buffer_2_out, buffer_1_out);
  D_Flip_Flop store_0 (.D(and_1_out), .clk(buffer_2_out), .Q(store_0_q));  // open: Qn, preset, reset
  D_Flip_Flop store_1 (.D(and_2_out), .clk(buffer_2_out), .Q(store_1_q));  // open: Qn, preset, reset
  D_Flip_Flop store_2 (.D(and_3_out), .clk(buffer_2_out), .Q(store_2_q));  // open: Qn, preset, reset
  D_Flip_Flop store_3 (.D(and_4_out), .clk(buffer_2_out), .Q(store_3_q));  // open: Qn, preset, reset
  // Probe on store_2_q
  // Probe on store_3_q
  // Probe on store_1_q
  // Probe on store_0_q
  and and_5 (out_0, store_0_q, Read_en);
  and and_6 (out_1, store_1_q, Read_en);
  and and_7 (out_2, store_2_q, Read_en);
  and and_8 (out_3, store_3_q, Read_en);
endmodule

module address_register (
  input  Write_en,
  input  in_0,
  input  in_1,
  input  in_2,
  input  Read_en,
  output out_0,
  output out_1,
  output out_2
);

  wire and_1_out, and_2_out, and_3_out, buffer_1_out, buffer_2_out, store_0_q, store_1_q, store_2_q;

  and and_1 (and_1_out, in_0, Write_en);
  and and_2 (and_2_out, in_1, Write_en);
  and and_3 (and_3_out, in_2, Write_en);
  buf buffer_1 (buffer_1_out, Write_en);
  buf buffer_2 (buffer_2_out, buffer_1_out);
  D_Flip_Flop store_0 (.D(and_1_out), .clk(buffer_2_out), .Q(store_0_q));  // open: Qn, preset, reset
  D_Flip_Flop store_1 (.D(and_2_out), .clk(buffer_2_out), .Q(store_1_q));  // open: Qn, preset, reset
  D_Flip_Flop store_2 (.D(and_3_out), .clk(buffer_2_out), .Q(store_2_q));  // open: Qn, preset, reset
  // Probe on store_1_q
  // Probe on store_2_q
  // Probe on store_0_q
  and and_4 (out_0, store_0_q, Read_en);
  and and_5 (out_1, store_1_q, Read_en);
  and and_6 (out_2, store_2_q, Read_en);
endmodule

module output_register (
  input  Write_en,
  input  in_0,
  input  in_1,
  input  in_2,
  input  in_3,
  input  Read_en,
  output out_0,
  output out_1,
  output out_2,
  output out_3
);

  wire and_1_out, and_2_out, and_3_out, and_4_out, buffer_1_out, buffer_2_out, store_0_q, store_1_q,
       store_2_q, store_3_q;

  and and_1 (and_1_out, in_0, Write_en);
  and and_2 (and_2_out, in_1, Write_en);
  and and_3 (and_3_out, in_2, Write_en);
  and and_4 (and_4_out, in_3, Write_en);
  buf buffer_1 (buffer_1_out, Write_en);
  buf buffer_2 (buffer_2_out, buffer_1_out);
  D_Flip_Flop store_0 (.D(and_1_out), .clk(buffer_2_out), .Q(store_0_q));  // open: Qn, preset, reset
  D_Flip_Flop store_1 (.D(and_2_out), .clk(buffer_2_out), .Q(store_1_q));  // open: Qn, preset, reset
  D_Flip_Flop store_2 (.D(and_3_out), .clk(buffer_2_out), .Q(store_2_q));  // open: Qn, preset, reset
  D_Flip_Flop store_3 (.D(and_4_out), .clk(buffer_2_out), .Q(store_3_q));  // open: Qn, preset, reset
  // Probe on store_3_q
  // Probe on store_2_q
  // Probe on store_1_q
  // Probe on store_0_q
  and and_5 (out_0, store_0_q, Read_en);
  and and_6 (out_1, store_1_q, Read_en);
  and and_7 (out_2, store_2_q, Read_en);
  and and_8 (out_3, store_3_q, Read_en);
endmodule

module mux_3_to_8 (
  input  In0,
  input  In1,
  input  In2,
  output Out0,
  output Out1,
  output Out2,
  output Out3,
  output Out4,
  output Out5,
  output Out6,
  output Out7
);

  wire buffer_1_out, buffer_2_out, buffer_3_out, not_1_out, not_2_out, not_3_out;

  buf buffer_1 (buffer_1_out, In0);
  buf buffer_2 (buffer_2_out, In1);
  buf buffer_3 (buffer_3_out, In2);
  not not_1 (not_1_out, In0);
  not not_2 (not_2_out, In1);
  not not_3 (not_3_out, In2);
  and and_1 (Out0, not_3_out, not_2_out, not_1_out);
  and and_2 (Out1, not_3_out, not_2_out, buffer_1_out);
  and and_3 (Out2, not_3_out, buffer_2_out, not_1_out);
  and and_4 (Out3, not_3_out, buffer_2_out, buffer_1_out);
  and and_5 (Out4, buffer_3_out, not_2_out, not_1_out);
  and and_6 (Out5, buffer_3_out, not_2_out, buffer_1_out);
  and and_7 (Out6, buffer_3_out, buffer_2_out, not_1_out);
  and and_8 (Out7, buffer_3_out, buffer_2_out, buffer_1_out);
endmodule

module Ram_select (
  input  In0,
  input  In1,
  input  In2,
  input  In3,
  input  read_en,
  input  address,
  input  mode,
  output Out0,
  output Out1,
  output Out2,
  output Out3
);

  wire and_1_out;

  and and_1 (and_1_out, read_en, address, mode);
  and and_2 (Out0, In0, and_1_out);
  and and_3 (Out1, In1, and_1_out);
  and and_4 (Out2, In2, and_1_out);
  and and_5 (Out3, In3, and_1_out);
endmodule

module RAM_4bit (
  input  d3,
  input  d2,
  input  d1,
  input  d0,
  input  Write_to_AR_MR,
  input  Write_to_Din,
  input  Reg_to_Ram,
  input  Write_Ram_to_Dout,
  input  Read_Dout,
  input  Mode,
  input  a2,
  input  a1,
  input  a0,
  output R0_3,
  output R0_2,
  output R0_1,
  output R0_0,
  output out3,
  output out2,
  output out1,
  output out0
);

  wire and_1_out, and_2_out, and_3_out, and_4_out, and_5_out, and_6_out, and_7_out, and_8_out, AR0, AR1, AR2,
       buffer_1_out, buffer_2_out, buffer_3_out, buffer_4_out, buffer_5_out, buffer_6_out, buffer_7_out,
       buffer_8_out, buffer_9_out, buffer_10_out, buffer_11_out, buffer_12_out, buffer_13_out, buffer_14_out,
       buffer_15_out, buffer_16_out, buffer_17_out, buffer_18_out, buffer_19_out, buffer_20_out,
       buffer_21_out, buffer_22_out, buffer_23_out, buffer_24_out, buffer_25_out, buffer_26_out,
       buffer_27_out, buffer_28_out, input_register_1_out_0, input_register_1_out_1, input_register_1_out_2,
       input_register_1_out_3, MR, mux_3_to_8_1_out0, mux_3_to_8_1_out1, mux_3_to_8_1_out2,
       mux_3_to_8_1_out3, mux_3_to_8_1_out4, mux_3_to_8_1_out5, mux_3_to_8_1_out6, mux_3_to_8_1_out7,
       mux_3_to_8_2_out0, mux_3_to_8_2_out1, mux_3_to_8_2_out2, mux_3_to_8_2_out3, mux_3_to_8_2_out4,
       mux_3_to_8_2_out5, mux_3_to_8_2_out6, mux_3_to_8_2_out7, nibble_1_out_0, nibble_1_out_1,
       nibble_1_out_2, nibble_1_out_3, nibble_3_out_0, nibble_3_out_1, nibble_3_out_2, nibble_3_out_3,
       nibble_4_out_0, nibble_4_out_1, nibble_4_out_2, nibble_4_out_3, nibble_5_out_0, nibble_5_out_1,
       nibble_5_out_2, nibble_5_out_3, nibble_6_out_0, nibble_6_out_1, nibble_6_out_2, nibble_6_out_3,
       nibble_7_out_0, nibble_7_out_1, nibble_7_out_2, nibble_7_out_3, nibble_8_out_0, nibble_8_out_1,
       nibble_8_out_2, nibble_8_out_3, or_1_out, or_2_out, or_3_out, or_4_out, or_5_out, or_6_out, or_7_out,
       or_8_out, or_9_out, or_10_out, or_11_out, or_12_out, or_13_out, or_14_out, or_15_out, or_16_out,
       or_17_out, or_18_out, or_19_out, or_20_out, or_21_out, or_22_out, or_23_out, or_24_out, or_25_out,
       or_26_out, or_27_out, or_28_out, or_29_out, ram_select_1_out0, ram_select_1_out1, ram_select_1_out2,
       ram_select_1_out3, ram_select_2_out0, ram_select_2_out1, ram_select_2_out2, ram_select_2_out3,
       ram_select_3_out0, ram_select_3_out1, ram_select_3_out2, ram_select_3_out3, ram_select_4_out0,
       ram_select_4_out1, ram_select_4_out2, ram_select_4_out3, ram_select_5_out0, ram_select_5_out1,
       ram_select_5_out2, ram_select_5_out3, ram_select_6_out0, ram_select_6_out1, ram_select_6_out2,
       ram_select_6_out3, ram_select_7_out0, ram_select_7_out1, ram_select_7_out2, ram_select_7_out3,
       ram_select_8_out0, ram_select_8_out1, ram_select_8_out2, ram_select_8_out3;

  or or_1 (or_1_out, Write_Ram_to_Dout, Reg_to_Ram);
  mode_register mode_register_1 (.out_0(MR), .Write_en(Write_to_AR_MR), .in_0(Mode), .Read_en(or_1_out));
  address_register address_register_1 (
    .out_0(AR0), .out_1(AR1), .out_2(AR2), .Write_en(Write_to_AR_MR), .in_0(a0), .in_1(a1), .in_2(a2),
    .Read_en(or_1_out));
  mux_3_to_8 mux_3_to_8_1 (
    .Out2(mux_3_to_8_1_out2), .Out3(mux_3_to_8_1_out3), .Out4(mux_3_to_8_1_out4), .Out5(mux_3_to_8_1_out5),
    .Out6(mux_3_to_8_1_out6), .Out7(mux_3_to_8_1_out7), .Out0(mux_3_to_8_1_out0), .Out1(mux_3_to_8_1_out1),
    .In2(AR2), .In0(AR0), .In1(AR1));
  buf buffer_1 (buffer_1_out, Reg_to_Ram);
  buf buffer_2 (buffer_2_out, buffer_1_out);
  buf buffer_3 (buffer_3_out, buffer_2_out);
  buf buffer_4 (buffer_4_out, buffer_3_out);
  buf buffer_5 (buffer_5_out, buffer_4_out);
  buf buffer_6 (buffer_6_out, buffer_5_out);
  buf buffer_7 (buffer_7_out, buffer_6_out);
  buf buffer_8 (buffer_8_out, buffer_7_out);
  and and_1 (and_1_out, mux_3_to_8_1_out0, ~MR, buffer_8_out);  // AND_Gate
  and and_2 (and_2_out, mux_3_to_8_1_out1, ~MR, buffer_8_out);  // AND_Gate
  and and_3 (and_3_out, mux_3_to_8_1_out2, ~MR, buffer_8_out);  // AND_Gate
  and and_4 (and_4_out, mux_3_to_8_1_out3, ~MR, buffer_8_out);  // AND_Gate
  and and_5 (and_5_out, mux_3_to_8_1_out5, ~MR, buffer_8_out);  // AND_Gate
  and and_6 (and_6_out, mux_3_to_8_1_out6, ~MR, buffer_8_out);  // AND_Gate
  and and_7 (and_7_out, mux_3_to_8_1_out7, ~MR, buffer_8_out);  // AND_Gate
  and and_8 (and_8_out, mux_3_to_8_1_out4, ~MR, buffer_8_out);  // AND_Gate
  input_register input_register_1 (
    .out_0(input_register_1_out_0), .out_1(input_register_1_out_1), .out_2(input_register_1_out_2),
    .out_3(input_register_1_out_3), .Write_en(Write_to_Din), .in_0(d0), .in_1(d1), .in_2(d2), .in_3(d3),
    .Read_en(Reg_to_Ram));
  Nibble nibble_1 (
    .out_0(nibble_1_out_0), .out_1(nibble_1_out_1), .out_2(nibble_1_out_2), .out_3(nibble_1_out_3),
    .Write_en(and_2_out), .in_0(input_register_1_out_0), .in_1(input_register_1_out_1),
    .in_2(input_register_1_out_2), .in_3(input_register_1_out_3));
  Nibble nibble_2 (
    .out_0(R0_0), .out_1(R0_1), .out_2(R0_2), .out_3(R0_3), .Write_en(and_1_out),
    .in_0(input_register_1_out_0), .in_1(input_register_1_out_1), .in_2(input_register_1_out_2),
    .in_3(input_register_1_out_3));
  Nibble nibble_3 (
    .out_0(nibble_3_out_0), .out_1(nibble_3_out_1), .out_2(nibble_3_out_2), .out_3(nibble_3_out_3),
    .Write_en(and_3_out), .in_0(input_register_1_out_0), .in_1(input_register_1_out_1),
    .in_2(input_register_1_out_2), .in_3(input_register_1_out_3));
  Nibble nibble_4 (
    .out_0(nibble_4_out_0), .out_1(nibble_4_out_1), .out_2(nibble_4_out_2), .out_3(nibble_4_out_3),
    .Write_en(and_4_out), .in_0(input_register_1_out_0), .in_1(input_register_1_out_1),
    .in_2(input_register_1_out_2), .in_3(input_register_1_out_3));
  Nibble nibble_5 (
    .out_0(nibble_5_out_0), .out_1(nibble_5_out_1), .out_2(nibble_5_out_2), .out_3(nibble_5_out_3),
    .Write_en(and_8_out), .in_0(input_register_1_out_0), .in_1(input_register_1_out_1),
    .in_2(input_register_1_out_2), .in_3(input_register_1_out_3));
  Nibble nibble_6 (
    .out_0(nibble_6_out_0), .out_1(nibble_6_out_1), .out_2(nibble_6_out_2), .out_3(nibble_6_out_3),
    .Write_en(and_5_out), .in_0(input_register_1_out_0), .in_1(input_register_1_out_1),
    .in_2(input_register_1_out_2), .in_3(input_register_1_out_3));
  Nibble nibble_7 (
    .out_0(nibble_7_out_0), .out_1(nibble_7_out_1), .out_2(nibble_7_out_2), .out_3(nibble_7_out_3),
    .Write_en(and_6_out), .in_0(input_register_1_out_0), .in_1(input_register_1_out_1),
    .in_2(input_register_1_out_2), .in_3(input_register_1_out_3));
  Nibble nibble_8 (
    .out_0(nibble_8_out_0), .out_1(nibble_8_out_1), .out_2(nibble_8_out_2), .out_3(nibble_8_out_3),
    .Write_en(and_7_out), .in_0(input_register_1_out_0), .in_1(input_register_1_out_1),
    .in_2(input_register_1_out_2), .in_3(input_register_1_out_3));
  mux_3_to_8 mux_3_to_8_2 (
    .Out2(mux_3_to_8_2_out2), .Out3(mux_3_to_8_2_out3), .Out4(mux_3_to_8_2_out4), .Out5(mux_3_to_8_2_out5),
    .Out6(mux_3_to_8_2_out6), .Out7(mux_3_to_8_2_out7), .Out0(mux_3_to_8_2_out0), .Out1(mux_3_to_8_2_out1),
    .In2(AR2), .In0(AR0), .In1(AR1));
  // Probe on R0_3
  // Probe on nibble_1_out_3
  // Probe on R0_2
  // Probe on R0_1
  // Probe on nibble_1_out_2
  // Probe on nibble_1_out_1
  // Probe on nibble_3_out_3
  // Probe on nibble_3_out_2
  // Probe on nibble_4_out_3
  // Probe on nibble_4_out_2
  // Probe on nibble_5_out_3
  // Probe on nibble_5_out_2
  // Probe on nibble_6_out_3
  // Probe on nibble_6_out_2
  // Probe on nibble_7_out_3
  // Probe on nibble_7_out_2
  // Probe on nibble_8_out_3
  // Probe on nibble_8_out_2
  // Probe on R0_0
  // Probe on nibble_1_out_0
  // Probe on nibble_3_out_1
  // Probe on nibble_3_out_0
  // Probe on nibble_4_out_1
  // Probe on nibble_4_out_0
  // Probe on nibble_5_out_1
  // Probe on nibble_5_out_0
  // Probe on nibble_6_out_1
  // Probe on nibble_6_out_0
  // Probe on nibble_7_out_1
  // Probe on nibble_7_out_0
  // Probe on nibble_8_out_1
  // Probe on nibble_8_out_0
  buf buffer_9 (buffer_9_out, buffer_10_out);
  buf buffer_10 (buffer_10_out, buffer_12_out);
  buf buffer_11 (buffer_11_out, buffer_9_out);
  buf buffer_12 (buffer_12_out, buffer_14_out);
  buf buffer_13 (buffer_13_out, buffer_11_out);
  buf buffer_14 (buffer_14_out, buffer_16_out);
  buf buffer_15 (buffer_15_out, buffer_13_out);
  buf buffer_16 (buffer_16_out, buffer_18_out);
  buf buffer_17 (buffer_17_out, buffer_15_out);
  buf buffer_18 (buffer_18_out, buffer_20_out);
  buf buffer_19 (buffer_19_out, buffer_17_out);
  buf buffer_20 (buffer_20_out, buffer_22_out);
  buf buffer_21 (buffer_21_out, buffer_19_out);
  buf buffer_22 (buffer_22_out, buffer_24_out);
  buf buffer_23 (buffer_23_out, buffer_21_out);
  buf buffer_24 (buffer_24_out, buffer_26_out);
  buf buffer_25 (buffer_25_out, buffer_23_out);
  buf buffer_26 (buffer_26_out, Write_Ram_to_Dout);
  buf buffer_27 (buffer_27_out, buffer_25_out);
  buf buffer_28 (buffer_28_out, buffer_27_out);
  Ram_select ram_select_1 (
    .In0(R0_0), .In1(R0_1), .In2(R0_2), .In3(R0_3), .read_en(Write_Ram_to_Dout), .address(mux_3_to_8_2_out0),
    .mode(MR), .Out0(ram_select_1_out0), .Out1(ram_select_1_out1), .Out2(ram_select_1_out2),
    .Out3(ram_select_1_out3));
  Ram_select ram_select_2 (
    .In0(nibble_1_out_0), .In1(nibble_1_out_1), .In2(nibble_1_out_2), .In3(nibble_1_out_3),
    .read_en(Write_Ram_to_Dout), .address(mux_3_to_8_2_out1), .mode(MR), .Out0(ram_select_2_out0),
    .Out1(ram_select_2_out1), .Out2(ram_select_2_out2), .Out3(ram_select_2_out3));
  Ram_select ram_select_3 (
    .In0(nibble_3_out_0), .In1(nibble_3_out_1), .In2(nibble_3_out_2), .In3(nibble_3_out_3),
    .read_en(Write_Ram_to_Dout), .address(mux_3_to_8_2_out2), .mode(MR), .Out0(ram_select_3_out0),
    .Out1(ram_select_3_out1), .Out2(ram_select_3_out2), .Out3(ram_select_3_out3));
  Ram_select ram_select_4 (
    .In0(nibble_4_out_0), .In1(nibble_4_out_1), .In2(nibble_4_out_2), .In3(nibble_4_out_3),
    .read_en(Write_Ram_to_Dout), .address(mux_3_to_8_2_out3), .mode(MR), .Out0(ram_select_4_out0),
    .Out1(ram_select_4_out1), .Out2(ram_select_4_out2), .Out3(ram_select_4_out3));
  Ram_select ram_select_5 (
    .In0(nibble_5_out_0), .In1(nibble_5_out_1), .In2(nibble_5_out_2), .In3(nibble_5_out_3),
    .read_en(Write_Ram_to_Dout), .address(mux_3_to_8_2_out4), .mode(MR), .Out0(ram_select_5_out0),
    .Out1(ram_select_5_out1), .Out2(ram_select_5_out2), .Out3(ram_select_5_out3));
  Ram_select ram_select_6 (
    .In0(nibble_6_out_0), .In1(nibble_6_out_1), .In2(nibble_6_out_2), .In3(nibble_6_out_3),
    .read_en(Write_Ram_to_Dout), .address(mux_3_to_8_2_out5), .mode(MR), .Out0(ram_select_6_out0),
    .Out1(ram_select_6_out1), .Out2(ram_select_6_out2), .Out3(ram_select_6_out3));
  Ram_select ram_select_7 (
    .In0(nibble_7_out_0), .In1(nibble_7_out_1), .In2(nibble_7_out_2), .In3(nibble_7_out_3),
    .read_en(Write_Ram_to_Dout), .address(mux_3_to_8_2_out6), .mode(MR), .Out0(ram_select_7_out0),
    .Out1(ram_select_7_out1), .Out2(ram_select_7_out2), .Out3(ram_select_7_out3));
  Ram_select ram_select_8 (
    .In0(nibble_8_out_0), .In1(nibble_8_out_1), .In2(nibble_8_out_2), .In3(nibble_8_out_3),
    .read_en(Write_Ram_to_Dout), .address(mux_3_to_8_2_out7), .mode(MR), .Out0(ram_select_8_out0),
    .Out1(ram_select_8_out1), .Out2(ram_select_8_out2), .Out3(ram_select_8_out3));
  or or_2 (or_2_out, or_3_out, ram_select_1_out3);
  or or_3 (or_3_out, or_4_out, ram_select_2_out3);
  or or_4 (or_4_out, or_5_out, ram_select_3_out3);
  or or_5 (or_5_out, or_6_out, ram_select_4_out3);
  or or_6 (or_6_out, or_7_out, ram_select_5_out3);
  or or_7 (or_7_out, or_8_out, ram_select_6_out3);
  or or_8 (or_8_out, ram_select_8_out3, ram_select_7_out3);
  or or_9 (or_9_out, or_10_out, ram_select_1_out2);
  or or_10 (or_10_out, or_11_out, ram_select_2_out2);
  or or_11 (or_11_out, or_12_out, ram_select_3_out2);
  or or_12 (or_12_out, or_13_out, ram_select_4_out2);
  or or_13 (or_13_out, or_14_out, ram_select_5_out2);
  or or_14 (or_14_out, or_15_out, ram_select_6_out2);
  or or_15 (or_15_out, ram_select_8_out2, ram_select_7_out2);
  output_register output_register_1 (
    .out_0(out0), .out_1(out1), .out_2(out2), .out_3(out3), .Read_en(Read_Dout), .Write_en(buffer_28_out),
    .in_0(or_23_out), .in_1(or_16_out), .in_2(or_9_out), .in_3(or_2_out));
  or or_16 (or_16_out, or_17_out, ram_select_1_out1);
  or or_17 (or_17_out, or_18_out, ram_select_2_out1);
  or or_18 (or_18_out, or_19_out, ram_select_3_out1);
  or or_19 (or_19_out, or_20_out, ram_select_4_out1);
  or or_20 (or_20_out, or_21_out, ram_select_5_out1);
  or or_21 (or_21_out, or_22_out, ram_select_6_out1);
  or or_22 (or_22_out, ram_select_8_out1, ram_select_7_out1);
  or or_23 (or_23_out, or_24_out, ram_select_1_out0);
  or or_24 (or_24_out, or_25_out, ram_select_2_out0);
  or or_25 (or_25_out, or_26_out, ram_select_3_out0);
  or or_26 (or_26_out, or_27_out, ram_select_4_out0);
  or or_27 (or_27_out, or_28_out, ram_select_5_out0);
  or or_28 (or_28_out, or_29_out, ram_select_6_out0);
  or or_29 (or_29_out, ram_select_8_out0, ram_select_7_out0);

  // Other names for the same wires on the sheet: RD = Read_Dout; WRTD = Write_Ram_to_Dout

  // Notes on the sheet:
  //   Jiahang Wang 261011319
  //   Save 1 / Load 1
  //   Save 2
  //   Save 3
  //   Load 2
  //   Load 3
  //   3-bit address input pins
  //   4-bit data input pins
  //   Mode Input Register
  //   Address Input Register
  //   RAM
  //   Data Input Register
  //   Address:0
  //   Address:1
  //   Address:2
  //   Address:3
  //   Address:4
  //   Address:5
  //   Address:6
  //   Address:7
  //   0ut_3
  //   Data Register
  //   0ut_2
  //   0ut_1
  //   0ut_0
  //   4-bit data output pins
endmodule

module adder_4 (
  input  n1_3,
  input  n1_2,
  input  n1_1,
  input  n1_0,
  input  Enable,
  input  n2_3,
  input  n2_2,
  input  n2_1,
  input  n2_0,
  output s_3,
  output s_2,
  output s_1,
  output s_0,
  output overflow
);

  wire and_1_out, and_2_out, and_3_out, and_4_out, and_5_out, and_6_out, and_7_out, and_8_out, and_9_out,
       and_10_out, and_11_out, and_12_out, and_13_out, half_adder_1_carry_out, half_adder_2_carry_out,
       half_adder_3_carry_out, or_1_out;

  and and_1 (and_1_out, Enable, n2_3);
  and and_2 (and_2_out, Enable, n2_2);
  and and_3 (and_3_out, Enable, n2_1);
  and and_4 (and_4_out, Enable, n2_0);
  and and_5 (and_5_out, Enable, n1_3);
  and and_6 (and_6_out, Enable, n1_2);
  and and_7 (and_7_out, Enable, n1_1);
  and and_8 (and_8_out, Enable, n1_0);
  and and_9 (and_9_out, ~and_5_out, ~and_1_out);  // AND_Gate
  and and_10 (and_10_out, and_5_out, and_1_out);
  and and_11 (and_11_out, and_9_out, s_3);
  half_adder half_adder_1 (
    .Bit_1(and_8_out), .Bit_2(and_4_out), .sum(s_0), .carry_out(half_adder_1_carry_out));  // open: carry_in
  half_adder half_adder_2 (
    .Bit_1(and_7_out), .Bit_2(and_3_out), .carry_in(half_adder_1_carry_out), .sum(s_1),
    .carry_out(half_adder_2_carry_out));
  half_adder half_adder_3 (
    .Bit_1(and_6_out), .Bit_2(and_2_out), .carry_in(half_adder_2_carry_out), .sum(s_2),
    .carry_out(half_adder_3_carry_out));
  half_adder half_adder_4 (
    .Bit_1(and_5_out), .Bit_2(and_1_out), .carry_in(half_adder_3_carry_out), .sum(s_3));  // open: carry_out
  and and_12 (and_12_out, and_10_out, ~s_3);  // AND_Gate
  and and_13 (and_13_out, s_3, ~s_2, ~s_1, ~s_0);  // AND_Gate
  or or_1 (or_1_out, and_13_out, and_12_out);
  or or_2 (overflow, and_11_out, or_1_out);
endmodule

module half_adder (
  input  Bit_1,
  input  Bit_2,
  input  carry_in,
  output sum,
  output carry_out
);

  wire and_1_out, and_2_out, and_3_out, and_4_out, and_5_out, and_6_out, and_7_out, and_8_out, not_1_out,
       not_2_out, not_3_out;

  not not_1 (not_1_out, Bit_1);
  not not_2 (not_2_out, Bit_2);
  not not_3 (not_3_out, carry_in);
  and and_1 (and_1_out, Bit_1, not_2_out, not_3_out);
  and and_2 (and_2_out, not_1_out, Bit_2, not_3_out);
  and and_3 (and_3_out, not_1_out, not_2_out, carry_in);
  and and_4 (and_4_out, Bit_1, Bit_2, carry_in);
  and and_5 (and_5_out, Bit_1, Bit_2, not_3_out);
  and and_6 (and_6_out, Bit_1, not_2_out, carry_in);
  and and_7 (and_7_out, not_1_out, Bit_2, carry_in);
  and and_8 (and_8_out, Bit_1, Bit_2, carry_in);
  or or_1 (sum, and_1_out, and_2_out, and_3_out, and_4_out);
  or or_2 (carry_out, and_5_out, and_6_out, and_7_out, and_8_out);
endmodule

module complement_2 (
  input  In3,
  input  In2,
  input  In1,
  input  In0,
  input  mode,
  output out_3,
  output out_2,
  output out_1,
  output out_0
);

  wire adder_4_1_s_0, adder_4_1_s_1, adder_4_1_s_2, adder_4_1_s_3, and_1_out, and_2_out, and_3_out,
       and_4_out, and_5_out, and_6_out, and_7_out, and_8_out, not_1_out, not_2_out, not_3_out, not_4_out;

  and and_1 (and_1_out, In3, ~mode);  // AND_Gate
  or or_1 (out_3, and_1_out, adder_4_1_s_3);
  and and_2 (and_2_out, In2, ~mode);  // AND_Gate
  or or_2 (out_2, and_2_out, adder_4_1_s_2);
  and and_3 (and_3_out, In1, ~mode);  // AND_Gate
  or or_3 (out_1, and_3_out, adder_4_1_s_1);
  and and_4 (and_4_out, In0, ~mode);  // AND_Gate
  or or_4 (out_0, and_4_out, adder_4_1_s_0);
  and and_5 (and_5_out, In0, mode);
  not not_1 (not_1_out, and_5_out);
  and and_6 (and_6_out, In1, mode);
  not not_2 (not_2_out, and_6_out);
  and and_7 (and_7_out, In3, mode);
  and and_8 (and_8_out, In2, mode);
  not not_3 (not_3_out, and_7_out);
  not not_4 (not_4_out, and_8_out);
  adder_4 adder_4_1 (
    .n1_3(not_3_out), .n1_2(not_4_out), .n1_1(not_2_out), .n1_0(not_1_out), .Enable(mode), .n2_0(mode),
    .s_3(adder_4_1_s_3), .s_2(adder_4_1_s_2), .s_1(adder_4_1_s_1), .s_0(adder_4_1_s_0));  // open: n2_3, n2_2, n2_1, overflow
endmodule

module L_R_register (
  input  In_0,
  input  In_1,
  input  In_2,
  input  In_3,
  input  Write_en,
  input  Read_en,
  output Out_0,
  output Out_1,
  output Out_2,
  output Out_3
);

  wire and_1_out, and_2_out, and_3_out, and_4_out, buffer_1_out, buffer_2_out, store_0_q, store_1_q,
       store_2_q, store_3_q;

  buf buffer_1 (buffer_1_out, Write_en);
  and and_1 (and_1_out, In_0, Write_en);
  and and_2 (and_2_out, In_1, Write_en);
  and and_3 (and_3_out, In_2, Write_en);
  and and_4 (and_4_out, In_3, Write_en);
  buf buffer_2 (buffer_2_out, buffer_1_out);
  D_Flip_Flop store_0 (.D(and_1_out), .clk(buffer_2_out), .Q(store_0_q));  // open: Qn, preset, reset
  D_Flip_Flop store_1 (.D(and_2_out), .clk(buffer_2_out), .Q(store_1_q));  // open: Qn, preset, reset
  D_Flip_Flop store_2 (.D(and_3_out), .clk(buffer_2_out), .Q(store_2_q));  // open: Qn, preset, reset
  D_Flip_Flop store_3 (.D(and_4_out), .clk(buffer_2_out), .Q(store_3_q));  // open: Qn, preset, reset
  // Probe on store_3_q
  // Probe on store_2_q
  // Probe on store_1_q
  // Probe on store_0_q
  and and_5 (Out_0, store_0_q, Read_en);
  and and_6 (Out_1, store_1_q, Read_en);
  and and_7 (Out_2, store_2_q, Read_en);
  and and_8 (Out_3, store_3_q, Read_en);
endmodule

module status_register (
  input  In_0,
  input  In_1,
  input  In_2,
  input  In_3,
  input  Write_en,
  input  Read_en,
  output Out_0,
  output Out_1,
  output Out_2,
  output Out_3
);

  wire and_1_out, and_2_out, and_3_out, and_4_out, buffer_1_out, buffer_2_out, negative_q, overflow_q,
       signed_overflow_q, zero_q;

  and and_1 (and_1_out, In_0, Write_en);
  and and_2 (and_2_out, In_1, Write_en);
  and and_3 (and_3_out, In_2, Write_en);
  and and_4 (and_4_out, In_3, Write_en);
  buf buffer_1 (buffer_1_out, Write_en);
  buf buffer_2 (buffer_2_out, buffer_1_out);
  D_Flip_Flop negative (.D(and_1_out), .clk(buffer_2_out), .Q(negative_q));  // open: Qn, preset, reset
  D_Flip_Flop zero (.D(and_2_out), .clk(buffer_2_out), .Q(zero_q));  // open: Qn, preset, reset
  D_Flip_Flop overflow (.D(and_3_out), .clk(buffer_2_out), .Q(overflow_q));  // open: Qn, preset, reset
  D_Flip_Flop signed_overflow (.D(and_4_out), .clk(buffer_2_out), .Q(signed_overflow_q));  // open: Qn, preset, reset
  and and_5 (Out_0, negative_q, Read_en);
  and and_6 (Out_1, zero_q, Read_en);
  and and_7 (Out_2, overflow_q, Read_en);
  and and_8 (Out_3, signed_overflow_q, Read_en);
endmodule

module A_out_register (
  input  In_0,
  input  In_1,
  input  In_2,
  input  In_3,
  input  Write_en,
  input  Read_en,
  output Out_0,
  output Out_1,
  output Out_2,
  output Out_3
);

  wire and_1_out, and_2_out, and_3_out, and_4_out, buffer_1_out, buffer_2_out, store_0_q, store_1_q,
       store_2_q, store_3_q;

  and and_1 (and_1_out, In_0, Write_en);
  and and_2 (and_2_out, In_1, Write_en);
  and and_3 (and_3_out, In_2, Write_en);
  and and_4 (and_4_out, In_3, Write_en);
  buf buffer_1 (buffer_1_out, Write_en);
  buf buffer_2 (buffer_2_out, buffer_1_out);
  D_Flip_Flop store_0 (.D(and_1_out), .clk(buffer_2_out), .Q(store_0_q));  // open: Qn, preset, reset
  D_Flip_Flop store_1 (.D(and_2_out), .clk(buffer_2_out), .Q(store_1_q));  // open: Qn, preset, reset
  D_Flip_Flop store_2 (.D(and_3_out), .clk(buffer_2_out), .Q(store_2_q));  // open: Qn, preset, reset
  D_Flip_Flop store_3 (.D(and_4_out), .clk(buffer_2_out), .Q(store_3_q));  // open: Qn, preset, reset
  and and_5 (Out_0, store_0_q, Read_en);
  and and_6 (Out_1, store_1_q, Read_en);
  and and_7 (Out_2, store_2_q, Read_en);
  and and_8 (Out_3, store_3_q, Read_en);
endmodule

module ALU (
  input  L_3,
  input  L_2,
  input  L_1,
  input  L_0,
  input  R_3,
  input  R_2,
  input  R_1,
  input  R_0,
  input  Write_to_L_R_Reg,
  input  Reg_to_adder_to_Aout,
  input  Read_Aout_SR,
  input  Add_Sub_command,
  output negative,
  output zero,
  output overflow,
  output signed_overflow,
  output a_3,
  output a_2,
  output a_1,
  output a_0
);

  wire adder_4_1_overflow, adder_4_1_s_0, adder_4_1_s_1, adder_4_1_s_2, adder_4_1_s_3, and_1_out, and_2_out,
       and_3_out, and_4_out, buffer_1_out, buffer_2_out, buffer_3_out, buffer_4_out, buffer_5_out,
       buffer_6_out, buffer_7_out, buffer_8_out, buffer_9_out, buffer_10_out, buffer_11_out, buffer_12_out,
       buffer_13_out, buffer_14_out, buffer_15_out, buffer_16_out, buffer_17_out, buffer_18_out,
       buffer_19_out, buffer_20_out, buffer_21_out, buffer_22_out, buffer_23_out, buffer_24_out,
       buffer_25_out, buffer_26_out, buffer_27_out, buffer_28_out, buffer_29_out, buffer_30_out,
       buffer_31_out, buffer_32_out, buffer_33_out, buffer_34_out, buffer_35_out, buffer_36_out,
       buffer_37_out, buffer_38_out, buffer_39_out, buffer_40_out, buffer_41_out, buffer_42_out,
       buffer_43_out, buffer_44_out, buffer_45_out, buffer_46_out, buffer_47_out, buffer_48_out,
       buffer_49_out, buffer_50_out, buffer_51_out, buffer_52_out, buffer_53_out, buffer_54_out,
       buffer_55_out, buffer_56_out, buffer_57_out, buffer_58_out, buffer_59_out, buffer_60_out,
       buffer_61_out, buffer_62_out, buffer_63_out, buffer_64_out, buffer_65_out, buffer_66_out,
       buffer_67_out, buffer_68_out, buffer_69_out, buffer_70_out, buffer_71_out, buffer_72_out,
       buffer_73_out, buffer_74_out, buffer_75_out, buffer_76_out, buffer_77_out, buffer_78_out,
       buffer_79_out, buffer_80_out, buffer_81_out, buffer_82_out, buffer_83_out, buffer_84_out,
       buffer_85_out, buffer_86_out, complement_2_1_out_0, complement_2_1_out_1, complement_2_1_out_2,
       complement_2_1_out_3, l1, l2, l3, l4, l_r_register_2_out_0, l_r_register_2_out_1,
       l_r_register_2_out_2, l_r_register_2_out_3, not_1_out, not_2_out;

  buf buffer_1 (buffer_1_out, Reg_to_adder_to_Aout);
  buf buffer_2 (buffer_2_out, buffer_4_out);
  buf buffer_3 (buffer_3_out, buffer_1_out);
  buf buffer_4 (buffer_4_out, buffer_6_out);
  buf buffer_5 (buffer_5_out, buffer_3_out);
  buf buffer_6 (buffer_6_out, buffer_8_out);
  buf buffer_7 (buffer_7_out, buffer_5_out);
  buf buffer_8 (buffer_8_out, buffer_10_out);
  buf buffer_9 (buffer_9_out, buffer_7_out);
  buf buffer_10 (buffer_10_out, buffer_12_out);
  buf buffer_11 (buffer_11_out, buffer_9_out);
  buf buffer_12 (buffer_12_out, buffer_14_out);
  buf buffer_13 (buffer_13_out, buffer_11_out);
  buf buffer_14 (buffer_14_out, buffer_16_out);
  buf buffer_15 (buffer_15_out, buffer_13_out);
  buf buffer_16 (buffer_16_out, buffer_18_out);
  buf buffer_17 (buffer_17_out, buffer_15_out);
  buf buffer_18 (buffer_18_out, buffer_20_out);
  buf buffer_19 (buffer_19_out, buffer_17_out);
  buf buffer_20 (buffer_20_out, buffer_22_out);
  buf buffer_21 (buffer_21_out, buffer_19_out);
  buf buffer_22 (buffer_22_out, buffer_24_out);
  buf buffer_23 (buffer_23_out, buffer_21_out);
  buf buffer_24 (buffer_24_out, buffer_26_out);
  buf buffer_25 (buffer_25_out, buffer_23_out);
  buf buffer_26 (buffer_26_out, buffer_28_out);
  buf buffer_27 (buffer_27_out, buffer_25_out);
  buf buffer_28 (buffer_28_out, buffer_29_out);
  buf buffer_29 (buffer_29_out, buffer_27_out);
  buf buffer_30 (buffer_30_out, buffer_2_out);
  buf buffer_31 (buffer_31_out, buffer_30_out);
  buf buffer_32 (buffer_32_out, buffer_31_out);
  buf buffer_33 (buffer_33_out, buffer_32_out);
  buf buffer_34 (buffer_34_out, buffer_33_out);
  buf buffer_35 (buffer_35_out, buffer_34_out);
  buf buffer_36 (buffer_36_out, buffer_35_out);
  buf buffer_37 (buffer_37_out, buffer_36_out);
  buf buffer_38 (buffer_38_out, buffer_37_out);
  buf buffer_39 (buffer_39_out, buffer_38_out);
  buf buffer_40 (buffer_40_out, buffer_39_out);
  buf buffer_41 (buffer_41_out, buffer_40_out);
  buf buffer_42 (buffer_42_out, buffer_41_out);
  buf buffer_43 (buffer_43_out, buffer_42_out);
  L_R_register l_r_register_1 (
    .In_0(L_0), .In_1(L_1), .In_2(L_2), .In_3(L_3), .Write_en(Write_to_L_R_Reg),
    .Read_en(Reg_to_adder_to_Aout), .Out_0(l1), .Out_1(l2), .Out_2(l3), .Out_3(l4));
  A_out_register a_out_register_1 (
    .In_0(adder_4_1_s_0), .In_1(adder_4_1_s_1), .In_2(adder_4_1_s_2), .In_3(adder_4_1_s_3),
    .Write_en(buffer_43_out), .Read_en(Read_Aout_SR), .Out_0(a_0), .Out_1(a_1), .Out_2(a_2), .Out_3(a_3));
  L_R_register l_r_register_2 (
    .In_0(R_0), .In_1(R_1), .In_2(R_2), .In_3(R_3), .Write_en(Write_to_L_R_Reg),
    .Read_en(Reg_to_adder_to_Aout), .Out_0(l_r_register_2_out_0), .Out_1(l_r_register_2_out_1),
    .Out_2(l_r_register_2_out_2), .Out_3(l_r_register_2_out_3));
  complement_2 complement_2_1 (
    .In3(l_r_register_2_out_3), .In2(l_r_register_2_out_2), .In1(l_r_register_2_out_1),
    .In0(l_r_register_2_out_0), .mode(Add_Sub_command), .out_3(complement_2_1_out_3),
    .out_2(complement_2_1_out_2), .out_1(complement_2_1_out_1), .out_0(complement_2_1_out_0));
  adder_4 adder_4_1 (
    .n1_3(l4), .n1_2(l3), .n1_1(l2), .n1_0(l1), .Enable(Reg_to_adder_to_Aout), .n2_3(complement_2_1_out_3),
    .n2_2(complement_2_1_out_2), .n2_1(complement_2_1_out_1), .n2_0(complement_2_1_out_0),
    .s_3(adder_4_1_s_3), .s_2(adder_4_1_s_2), .s_1(adder_4_1_s_1), .s_0(adder_4_1_s_0),
    .overflow(adder_4_1_overflow));
  buf buffer_44 (buffer_44_out, Reg_to_adder_to_Aout);
  buf buffer_45 (buffer_45_out, buffer_44_out);
  buf buffer_46 (buffer_46_out, buffer_45_out);
  buf buffer_47 (buffer_47_out, buffer_48_out);
  buf buffer_48 (buffer_48_out, buffer_49_out);
  buf buffer_49 (buffer_49_out, buffer_56_out);
  buf buffer_50 (buffer_50_out, buffer_47_out);
  buf buffer_51 (buffer_51_out, buffer_50_out);
  buf buffer_52 (buffer_52_out, buffer_46_out);
  buf buffer_53 (buffer_53_out, buffer_52_out);
  buf buffer_54 (buffer_54_out, buffer_53_out);
  buf buffer_55 (buffer_55_out, buffer_54_out);
  buf buffer_56 (buffer_56_out, buffer_57_out);
  buf buffer_57 (buffer_57_out, buffer_58_out);
  buf buffer_58 (buffer_58_out, buffer_59_out);
  buf buffer_59 (buffer_59_out, buffer_68_out);
  buf buffer_60 (buffer_60_out, buffer_51_out);
  buf buffer_61 (buffer_61_out, buffer_60_out);
  buf buffer_62 (buffer_62_out, buffer_61_out);
  buf buffer_63 (buffer_63_out, buffer_62_out);
  and and_1 (and_1_out, ~adder_4_1_s_3, ~adder_4_1_s_2, ~adder_4_1_s_1, ~adder_4_1_s_0);  // AND_Gate
  buf buffer_64 (buffer_64_out, buffer_55_out);
  buf buffer_65 (buffer_65_out, buffer_64_out);
  buf buffer_66 (buffer_66_out, buffer_65_out);
  buf buffer_67 (buffer_67_out, buffer_66_out);
  buf buffer_68 (buffer_68_out, buffer_69_out);
  buf buffer_69 (buffer_69_out, buffer_70_out);
  buf buffer_70 (buffer_70_out, buffer_71_out);
  buf buffer_71 (buffer_71_out, buffer_78_out);
  buf buffer_72 (buffer_72_out, buffer_63_out);
  buf buffer_73 (buffer_73_out, buffer_72_out);
  buf buffer_74 (buffer_74_out, buffer_67_out);
  buf buffer_75 (buffer_75_out, buffer_74_out);
  buf buffer_76 (buffer_76_out, buffer_75_out);
  buf buffer_77 (buffer_77_out, buffer_76_out);
  buf buffer_78 (buffer_78_out, buffer_79_out);
  buf buffer_79 (buffer_79_out, buffer_80_out);
  buf buffer_80 (buffer_80_out, buffer_81_out);
  buf buffer_81 (buffer_81_out, buffer_85_out);
  and and_2 (and_2_out, adder_4_1_overflow, not_2_out, not_1_out);
  buf buffer_82 (buffer_82_out, buffer_77_out);
  buf buffer_83 (buffer_83_out, buffer_82_out);
  buf buffer_84 (buffer_84_out, buffer_83_out);
  buf buffer_85 (buffer_85_out, buffer_86_out);
  buf buffer_86 (buffer_86_out, buffer_84_out);
  and and_3 (and_3_out, complement_2_1_out_3, ~complement_2_1_out_2, ~complement_2_1_out_1, ~complement_2_1_out_0, Add_Sub_command);  // AND_Gate
  not not_1 (not_1_out, and_3_out);
  not not_2 (not_2_out, and_4_out);
  and and_4 (and_4_out, complement_2_1_out_3, complement_2_1_out_2, ~complement_2_1_out_1, ~complement_2_1_out_0, l4, l3, ~l2, ~l1, ~Add_Sub_command);  // AND_Gate
  status_register status_register_1 (
    .In_0(adder_4_1_s_3), .In_1(and_1_out), .In_2(and_2_out), .In_3(and_2_out), .Write_en(buffer_73_out),
    .Read_en(1'b1), .Out_0(negative), .Out_1(zero), .Out_2(overflow), .Out_3(signed_overflow));

  // Other names for the same wires on the sheet: RAS = Read_Aout_SR

  // Notes on the sheet:
  //   Jiahang Wang 261011319
  //   Calculate 1
  //   Calculate 2
  //   Calculate 3
  //   Left Register
  //   A out Register
  //   Right Register
  //   2's complement
  //   ALU
  //   adder
  //   Status Register
endmodule

module PC (
  input  increase_en,
  input  Read_en,
  output Out_3,
  output Out_2,
  output Out_1,
  output Out_0
);

  wire and_1_out, and_2_out, and_3_out, and_4_out, and_5_out, and_6_out, and_7_out, and_8_out, and_9_out,
       and_10_out, and_11_out, and_12_out, buffer_1_out, buffer_2_out, buffer_3_out, not_1_out, not_2_out,
       not_3_out, or_1_out, or_2_out, or_3_out, stored_bit_0_q, stored_bit_1_q, stored_bit_2_q,
       stored_bit_3_q;

  not not_1 (not_1_out, stored_bit_2_q);
  not not_2 (not_2_out, stored_bit_1_q);
  not not_3 (not_3_out, stored_bit_0_q);
  buf buffer_1 (buffer_1_out, increase_en);
  buf buffer_2 (buffer_2_out, buffer_1_out);
  buf buffer_3 (buffer_3_out, buffer_2_out);
  and and_1 (and_1_out, not_1_out, stored_bit_1_q, stored_bit_0_q, increase_en);
  and and_2 (and_2_out, stored_bit_2_q, not_2_out, not_3_out, increase_en);
  and and_3 (and_3_out, stored_bit_2_q, not_2_out, stored_bit_0_q, increase_en);
  and and_4 (and_4_out, stored_bit_2_q, stored_bit_1_q, not_3_out, increase_en);
  and and_5 (and_5_out, not_1_out, not_2_out, stored_bit_0_q, increase_en);
  and and_6 (and_6_out, not_1_out, stored_bit_1_q, not_3_out, increase_en);
  and and_7 (and_7_out, stored_bit_2_q, not_2_out, stored_bit_0_q, increase_en);
  and and_8 (and_8_out, stored_bit_2_q, stored_bit_1_q, not_3_out, increase_en);
  and and_9 (and_9_out, not_1_out, not_2_out, not_3_out, increase_en);
  and and_10 (and_10_out, not_1_out, stored_bit_1_q, not_3_out, increase_en);
  and and_11 (and_11_out, stored_bit_2_q, not_2_out, not_3_out, increase_en);
  and and_12 (and_12_out, stored_bit_2_q, stored_bit_1_q, not_3_out, increase_en);
  or or_1 (or_1_out, and_1_out, and_2_out, and_3_out, and_4_out);
  or or_2 (or_2_out, and_5_out, and_6_out, and_7_out, and_8_out);
  or or_3 (or_3_out, and_9_out, and_10_out, and_11_out, and_12_out);
  D_Flip_Flop stored_bit_3 (.Q(stored_bit_3_q));  // open: D, clk, Qn, preset, reset
  D_Flip_Flop stored_bit_2 (.D(or_1_out), .clk(buffer_3_out), .Q(stored_bit_2_q));  // open: Qn, preset, reset
  D_Flip_Flop stored_bit_1 (.D(or_2_out), .clk(buffer_3_out), .Q(stored_bit_1_q));  // open: Qn, preset, reset
  D_Flip_Flop stored_bit_0 (.D(or_3_out), .clk(buffer_3_out), .Q(stored_bit_0_q));  // open: Qn, preset, reset
  // Probe on stored_bit_3_q
  // Probe on stored_bit_2_q
  // Probe on stored_bit_0_q
  // Probe on stored_bit_1_q
  and and_13 (Out_3, stored_bit_3_q, Read_en);
  and and_14 (Out_2, stored_bit_2_q, Read_en);
  and and_15 (Out_1, stored_bit_1_q, Read_en);
  and and_16 (Out_0, stored_bit_0_q, Read_en);

  // Notes on the sheet:
  //   PC
  //   Current address stored in PC (address only use three bit)
endmodule

module combine (
  input  S3,
  input  S2,
  input  S1,
  input  S0,
  input  In3,
  input  In2,
  output mode,
  output MAR_R,
  output AR_MR_W,
  output IR_to_MBR,
  output R0_R,
  output MBR_R,
  output L_R_W,
  output RAM_to_DR,
  output DR_W,
  output re_to_Aout,
  output command,
  output REG_12_R,
  output PC_R,
  output MAR_W,
  output DR_R,
  output MBR_W,
  output IR_W,
  output PC_inc,
  output IR_R,
  output Reg_to_RAM,
  output R0_W,
  output Aout_R,
  output REG_12_W,
  output D_W
);

  wire and_1_out, and_2_out, and_3_out, and_4_out, and_5_out, and_6_out, and_7_out, and_8_out, and_9_out,
       and_10_out, and_11_out, and_12_out, and_13_out, and_14_out, and_15_out, and_16_out, and_17_out,
       and_18_out, and_19_out, and_20_out, and_21_out, and_22_out, and_23_out, and_24_out, and_25_out,
       and_26_out, and_27_out, and_28_out, and_29_out, and_30_out, and_31_out, and_32_out, and_33_out,
       and_34_out, and_35_out, and_36_out, and_37_out, and_38_out, and_39_out, and_40_out, and_41_out,
       and_42_out, and_43_out, and_44_out, and_45_out, and_46_out, and_47_out, and_48_out, buffer_1_out,
       buffer_2_out, buffer_3_out, buffer_4_out, buffer_5_out, buffer_6_out, buffer_7_out, buffer_8_out,
       buffer_9_out, buffer_10_out, buffer_11_out, buffer_12_out, buffer_13_out, buffer_14_out,
       buffer_15_out, buffer_16_out, buffer_17_out, buffer_18_out, buffer_19_out, buffer_20_out,
       buffer_21_out, buffer_22_out, buffer_23_out, buffer_24_out, buffer_25_out, buffer_26_out,
       buffer_27_out, buffer_28_out, buffer_29_out, buffer_30_out, buffer_40_out, buffer_41_out,
       buffer_42_out, buffer_43_out, buffer_44_out, buffer_45_out, not_1_out, not_2_out, not_3_out,
       not_4_out, not_5_out, not_6_out, not_7_out, not_8_out, not_9_out, not_10_out, not_11_out, not_12_out,
       not_13_out, not_14_out, not_15_out, not_16_out, not_17_out, or_1_out, or_2_out, or_3_out, or_4_out,
       or_5_out, or_6_out, or_7_out, or_8_out, or_9_out, or_10_out, or_16_out, or_17_out;

  buf buffer_1 (buffer_1_out, S3);
  buf buffer_2 (buffer_2_out, S0);
  buf buffer_3 (buffer_3_out, S2);
  buf buffer_4 (buffer_4_out, S1);
  buf buffer_5 (buffer_5_out, In2);
  buf buffer_6 (buffer_6_out, In3);
  not not_1 (not_1_out, S3);
  not not_2 (not_2_out, S2);
  not not_3 (not_3_out, S1);
  not not_4 (not_4_out, S0);
  not not_5 (not_5_out, In3);
  not not_6 (not_6_out, In2);
  and and_1 (and_1_out, not_1_out, buffer_3_out, buffer_4_out, buffer_2_out, not_5_out, not_6_out);
  buf buffer_7 (buffer_7_out, and_1_out);
  and and_2 (and_2_out, not_1_out, buffer_3_out, buffer_4_out, buffer_2_out, not_5_out, not_6_out);
  and and_3 (and_3_out, not_1_out, buffer_3_out, buffer_4_out, buffer_2_out, not_5_out, buffer_5_out);
  and and_4 (and_4_out, not_1_out, buffer_3_out, buffer_4_out, buffer_2_out, not_5_out, not_6_out);
  and and_5 (and_5_out, not_1_out, buffer_3_out, buffer_4_out, buffer_2_out, not_5_out, buffer_5_out);
  and and_6 (and_6_out, not_1_out, buffer_3_out, buffer_4_out, buffer_2_out, not_5_out, buffer_5_out);
  and and_7 (and_7_out, not_1_out, buffer_3_out, buffer_4_out, buffer_2_out, buffer_6_out, not_6_out);
  and and_8 (and_8_out, not_1_out, buffer_3_out, buffer_4_out, buffer_2_out, buffer_6_out, buffer_5_out);
  and and_9 (and_9_out, not_1_out, buffer_3_out, buffer_4_out, buffer_2_out, buffer_6_out, not_6_out);
  and and_10 (and_10_out, not_1_out, buffer_3_out, buffer_4_out, buffer_2_out, buffer_6_out, buffer_5_out);
  and and_11 (and_11_out, buffer_1_out, not_2_out, not_3_out, not_4_out, not_5_out, buffer_5_out);
  and and_12 (and_12_out, not_1_out, buffer_3_out, buffer_4_out, buffer_2_out, buffer_6_out, not_6_out);
  and and_13 (and_13_out, not_1_out, buffer_3_out, buffer_4_out, buffer_2_out, buffer_6_out, buffer_5_out);
  and and_14 (and_14_out, buffer_1_out, not_2_out, not_3_out, not_4_out, not_5_out, not_6_out);
  and and_15 (and_15_out, buffer_1_out, not_2_out, not_3_out, not_4_out, not_5_out, buffer_5_out);
  and and_16 (and_16_out, buffer_1_out, not_2_out, not_3_out, not_4_out, buffer_6_out, not_6_out);
  and and_17 (and_17_out, buffer_1_out, not_2_out, not_3_out, not_4_out, buffer_6_out, buffer_5_out);
  and and_18 (and_18_out, buffer_1_out, not_2_out, not_3_out, not_4_out, buffer_6_out, buffer_5_out);
  and and_19 (and_19_out, not_1_out, buffer_3_out, buffer_4_out, buffer_2_out, buffer_6_out, not_6_out);
  and and_20 (and_20_out, not_1_out, buffer_3_out, buffer_4_out, buffer_2_out, buffer_6_out, buffer_5_out);
  or or_1 (or_1_out, and_2_out, and_3_out);
  or or_2 (or_2_out, and_4_out, and_5_out);
  buf buffer_8 (buffer_8_out, and_6_out);
  or or_3 (or_3_out, and_7_out, and_8_out);
  or or_4 (or_4_out, and_9_out, and_10_out, and_11_out);
  or or_5 (or_5_out, and_12_out, and_13_out);
  buf buffer_9 (buffer_9_out, and_14_out);
  buf buffer_10 (buffer_10_out, and_15_out);
  or or_6 (or_6_out, and_16_out, and_17_out);
  buf buffer_11 (buffer_11_out, and_18_out);
  or or_7 (or_7_out, and_19_out, and_20_out);
  buf buffer_12 (buffer_12_out, S2);
  buf buffer_13 (buffer_13_out, S1);
  buf buffer_14 (buffer_14_out, S0);
  buf buffer_15 (buffer_15_out, In3);
  buf buffer_16 (buffer_16_out, In2);
  not not_7 (not_7_out, S3);
  not not_8 (not_8_out, S2);
  not not_9 (not_9_out, S1);
  not not_10 (not_10_out, S0);
  not not_11 (not_11_out, In3);
  not not_12 (not_12_out, In2);
  and and_21 (and_21_out, not_7_out, not_8_out, not_9_out, buffer_14_out);
  buf buffer_17 (buffer_17_out, and_21_out);
  and and_22 (and_22_out, not_7_out, not_8_out, not_9_out, buffer_14_out);
  and and_23 (and_23_out, not_7_out, buffer_12_out, buffer_13_out, not_10_out, not_11_out, not_12_out);
  or or_8 (or_8_out, and_22_out, and_23_out, and_24_out);
  and and_24 (and_24_out, not_7_out, buffer_12_out, buffer_13_out, not_10_out, not_11_out, buffer_16_out);
  and and_25 (and_25_out, not_7_out, not_8_out, buffer_13_out, not_10_out);
  buf buffer_18 (buffer_18_out, and_25_out);
  and and_26 (and_26_out, not_7_out, not_8_out, buffer_13_out, not_10_out);
  buf buffer_19 (buffer_19_out, and_26_out);
  and and_27 (and_27_out, not_7_out, not_8_out, buffer_13_out, not_10_out);
  buf buffer_20 (buffer_20_out, and_27_out);
  and and_28 (and_28_out, not_7_out, not_8_out, buffer_13_out, buffer_14_out);
  buf buffer_21 (buffer_21_out, and_28_out);
  and and_29 (and_29_out, not_7_out, buffer_12_out, not_9_out, not_10_out);
  buf buffer_22 (buffer_22_out, and_29_out);
  and and_30 (and_30_out, not_7_out, buffer_12_out, not_9_out, not_10_out);
  buf buffer_23 (buffer_23_out, and_30_out);
  and and_31 (and_31_out, not_7_out, buffer_12_out, not_9_out, buffer_14_out);
  buf buffer_24 (buffer_24_out, and_31_out);
  and and_32 (and_32_out, not_7_out, buffer_12_out, not_9_out, buffer_14_out);
  buf buffer_25 (buffer_25_out, and_32_out);
  and and_33 (and_33_out, not_7_out, buffer_12_out, buffer_13_out, not_10_out, not_11_out, not_12_out);
  and and_34 (and_34_out, not_7_out, buffer_12_out, buffer_13_out, not_10_out, not_11_out, buffer_16_out);
  and and_35 (and_35_out, not_7_out, buffer_12_out, buffer_13_out, not_10_out, buffer_15_out, not_12_out);
  and and_36 (and_36_out, not_7_out, buffer_12_out, buffer_13_out, not_10_out, buffer_15_out, buffer_16_out);
  and and_37 (and_37_out, not_7_out, buffer_12_out, buffer_13_out, not_10_out, not_11_out, not_12_out);
  or or_9 (or_9_out, and_37_out, and_38_out);
  and and_38 (and_38_out, not_7_out, buffer_12_out, buffer_13_out, not_10_out, not_11_out, buffer_16_out);
  or or_10 (or_10_out, and_33_out, and_34_out, and_35_out, and_36_out);
  buf buffer_26 (buffer_26_out, S3);
  buf buffer_27 (buffer_27_out, S1);
  buf buffer_28 (buffer_28_out, S0);
  buf buffer_29 (buffer_29_out, In3);
  buf buffer_30 (buffer_30_out, In2);
  or or_11 (mode, buffer_7_out, buffer_18_out);
  or or_12 (MAR_R, or_1_out, buffer_19_out);
  or or_13 (AR_MR_W, or_2_out, buffer_20_out);
  or or_14 (MBR_R, or_4_out, buffer_43_out, buffer_24_out);
  or or_15 (RAM_to_DR, buffer_9_out, buffer_21_out);
  not not_13 (not_13_out, S2);
  not not_14 (not_14_out, S1);
  not not_15 (not_15_out, S0);
  not not_16 (not_16_out, In3);
  not not_17 (not_17_out, In2);
  buf buffer_31 (IR_to_MBR, buffer_8_out);
  buf buffer_32 (R0_R, or_3_out);
  buf buffer_33 (L_R_W, or_5_out);
  buf buffer_34 (DR_W, buffer_10_out);
  buf buffer_35 (re_to_Aout, or_6_out);
  buf buffer_36 (command, buffer_11_out);
  buf buffer_37 (REG_12_R, or_7_out);
  buf buffer_38 (PC_R, buffer_17_out);
  buf buffer_39 (MAR_W, or_8_out);
  and and_39 (and_39_out, buffer_26_out, not_13_out, not_14_out, buffer_28_out, not_16_out, not_17_out);
  buf buffer_40 (buffer_40_out, and_39_out);
  and and_40 (and_40_out, buffer_26_out, not_13_out, not_14_out, buffer_28_out, not_16_out, not_17_out);
  buf buffer_41 (buffer_41_out, and_40_out);
  and and_41 (and_41_out, buffer_26_out, not_13_out, not_14_out, buffer_28_out, not_16_out, buffer_30_out);
  buf buffer_42 (buffer_42_out, and_41_out);
  and and_42 (and_42_out, buffer_26_out, not_13_out, not_14_out, buffer_28_out, buffer_29_out, not_17_out);
  and and_43 (and_43_out, buffer_26_out, not_13_out, not_14_out, buffer_28_out, buffer_29_out, buffer_30_out);
  and and_44 (and_44_out, buffer_26_out, not_13_out, not_14_out, buffer_28_out, buffer_29_out, not_17_out);
  and and_45 (and_45_out, buffer_26_out, not_13_out, not_14_out, buffer_28_out, buffer_29_out, buffer_30_out);
  and and_46 (and_46_out, buffer_26_out, not_13_out, buffer_27_out, not_15_out, not_16_out, not_17_out);
  and and_47 (and_47_out, buffer_26_out, not_13_out, buffer_27_out, not_15_out, not_16_out, not_17_out);
  and and_48 (and_48_out, buffer_26_out, not_13_out, buffer_27_out, not_15_out, not_16_out, buffer_30_out);
  or or_16 (or_16_out, and_42_out, and_43_out);
  or or_17 (or_17_out, and_44_out, and_45_out);
  buf buffer_43 (buffer_43_out, and_46_out);
  buf buffer_44 (buffer_44_out, and_47_out);
  buf buffer_45 (buffer_45_out, and_48_out);
  or or_18 (MBR_W, buffer_23_out, buffer_40_out);
  or or_19 (DR_R, buffer_22_out, buffer_41_out);
  buf buffer_46 (IR_W, buffer_25_out);
  buf buffer_47 (PC_inc, or_10_out);
  buf buffer_48 (IR_R, or_9_out);
  buf buffer_49 (Reg_to_RAM, buffer_42_out);
  buf buffer_50 (R0_W, or_16_out);
  buf buffer_51 (Aout_R, or_17_out);
  buf buffer_52 (REG_12_W, buffer_44_out);
  buf buffer_53 (D_W, buffer_45_out);
endmodule

module det (
  input  clock,
  output out_2
);

  wire and_1_out, and_2_out, and_3_out, and_4_out, and_5_out, and_6_out, and_7_out, and_8_out, and_9_out,
       and_10_out, and_11_out, and_12_out, and_13_out, and_14_out, and_15_out, and_16_out, and_17_out,
       and_18_out, and_19_out, buffer_1_out, buffer_2_out, buffer_3_out, d_ff_1_q, d_ff_2_q, d_ff_3_q,
       d_ff_4_q, not_1_out, not_2_out, not_3_out, not_4_out, or_1_out, or_2_out, or_3_out, or_4_out;

  not not_1 (not_1_out, d_ff_1_q);
  not not_2 (not_2_out, d_ff_2_q);
  not not_3 (not_3_out, d_ff_3_q);
  not not_4 (not_4_out, d_ff_4_q);
  buf buffer_1 (buffer_1_out, clock);
  buf buffer_2 (buffer_2_out, buffer_1_out);
  buf buffer_3 (buffer_3_out, buffer_2_out);
  and and_1 (and_1_out, not_1_out, d_ff_2_q, d_ff_3_q, d_ff_4_q, clock);
  and and_2 (and_2_out, d_ff_1_q, not_2_out, not_3_out, not_4_out, clock);
  and and_3 (and_3_out, d_ff_1_q, not_2_out, not_3_out, d_ff_4_q, clock);
  and and_4 (and_4_out, not_1_out, not_2_out, d_ff_3_q, d_ff_4_q, clock);
  and and_5 (and_5_out, not_1_out, d_ff_2_q, not_3_out, not_4_out, clock);
  and and_6 (and_6_out, not_1_out, d_ff_2_q, not_3_out, d_ff_4_q, clock);
  and and_7 (and_7_out, not_1_out, d_ff_2_q, d_ff_3_q, not_4_out, clock);
  and and_8 (and_8_out, not_1_out, not_2_out, not_3_out, d_ff_4_q, clock);
  and and_9 (and_9_out, not_1_out, not_2_out, d_ff_3_q, not_4_out, clock);
  and and_10 (and_10_out, not_1_out, d_ff_2_q, not_3_out, d_ff_4_q, clock);
  and and_11 (and_11_out, not_1_out, d_ff_2_q, d_ff_3_q, not_4_out, clock);
  and and_12 (and_12_out, d_ff_1_q, not_2_out, not_3_out, d_ff_4_q, clock);
  and and_13 (and_13_out, not_1_out, not_2_out, not_3_out, not_4_out, clock);
  and and_14 (and_14_out, not_1_out, not_2_out, d_ff_3_q, not_4_out, clock);
  and and_15 (and_15_out, not_1_out, d_ff_2_q, not_3_out, not_4_out, clock);
  and and_16 (and_16_out, not_1_out, d_ff_2_q, d_ff_3_q, not_4_out, clock);
  and and_17 (and_17_out, d_ff_1_q, not_2_out, not_3_out, not_4_out, clock);
  and and_18 (and_18_out, d_ff_1_q, not_2_out, d_ff_3_q, not_4_out, clock);
  or or_1 (or_1_out, and_1_out, and_2_out, and_3_out);
  or or_2 (or_2_out, and_4_out, and_5_out, and_6_out, and_7_out);
  or or_3 (or_3_out, and_8_out, and_9_out, and_10_out, and_11_out, and_12_out);
  or or_4 (or_4_out, and_13_out, and_14_out, and_15_out, and_16_out, and_17_out, and_18_out);
  D_Flip_Flop d_ff_1 (.D(or_1_out), .clk(buffer_3_out), .Q(d_ff_1_q));  // open: Qn, preset, reset
  D_Flip_Flop d_ff_2 (.D(or_2_out), .clk(buffer_3_out), .Q(d_ff_2_q));  // open: Qn, preset, reset
  D_Flip_Flop d_ff_3 (.D(or_3_out), .clk(buffer_3_out), .Q(d_ff_3_q));  // open: Qn, preset, reset
  D_Flip_Flop d_ff_4 (.D(or_4_out), .clk(buffer_3_out), .Q(d_ff_4_q));  // open: Qn, preset, reset
  and and_19 (and_19_out, ~d_ff_1_q, d_ff_2_q, ~d_ff_3_q, d_ff_4_q);  // AND_Gate
  not not_5 (out_2, and_19_out);
endmodule

module CU (
  input  clock,
  input  In3,
  input  In2,
  input  In1,
  input  In0,
  output mode,
  output MAR_R,
  output AR_MR_W,
  output IR_to_MBR,
  output R0_R,
  output MBR_R,
  output L_R_W,
  output RAM_to_DR,
  output DR_W,
  output re_to_Aout,
  output command,
  output REG_12_R,
  output PC_R,
  output MAR_W,
  output DR_R,
  output MBR_W,
  output IR_W,
  output PC_inc,
  output IR_R,
  output Reg_to_RAM,
  output R0_W,
  output Aout_R,
  output REG_12_W,
  output D_W
);

  wire and_3_out, and_4_out, and_5_out, and_6_out, and_7_out, and_8_out, and_9_out, and_10_out, and_11_out,
       and_12_out, and_13_out, and_14_out, and_15_out, and_16_out, and_17_out, and_18_out, and_19_out,
       and_20_out, and_21_out, buffer_1_out, buffer_2_out, buffer_3_out, buffer_4_out, buffer_5_out,
       buffer_6_out, buffer_7_out, buffer_8_out, buffer_9_out, buffer_10_out, buffer_11_out, buffer_12_out,
       buffer_13_out, buffer_14_out, buffer_15_out, buffer_16_out, buffer_17_out, buffer_18_out,
       buffer_19_out, buffer_20_out, buffer_21_out, buffer_22_out, buffer_23_out, buffer_24_out, det_1_out_2,
       In_2, In_3, not_1_out, not_2_out, not_3_out, not_4_out, not_5_out, not_6_out, not_7_out, not_8_out,
       or_1_out, or_2_out, or_3_out, or_4_out, or_5_out, or_6_out, or_7_out, state_0_q, state_1_q, state_2_q,
       state_3_q;

  buf buffer_1 (buffer_1_out, clock);
  buf buffer_2 (buffer_2_out, buffer_1_out);
  buf buffer_3 (buffer_3_out, buffer_2_out);
  buf buffer_4 (buffer_4_out, buffer_5_out);
  buf buffer_5 (buffer_5_out, buffer_6_out);
  buf buffer_6 (buffer_6_out, buffer_11_out);
  buf buffer_7 (buffer_7_out, buffer_3_out);
  buf buffer_8 (buffer_8_out, buffer_7_out);
  buf buffer_9 (buffer_9_out, buffer_8_out);
  buf buffer_10 (buffer_10_out, buffer_9_out);
  buf buffer_11 (buffer_11_out, buffer_12_out);
  buf buffer_12 (buffer_12_out, buffer_13_out);
  buf buffer_13 (buffer_13_out, buffer_14_out);
  buf buffer_14 (buffer_14_out, buffer_10_out);
  det det_1 (.clock(clock), .out_2(det_1_out_2));
  buf buffer_15 (buffer_15_out, buffer_4_out);
  and and_1 (In_3, buffer_4_out, det_1_out_2, In3);
  and and_2 (In_2, buffer_4_out, det_1_out_2, In2);
  and and_3 (and_3_out, buffer_4_out, det_1_out_2, In1);
  and and_4 (and_4_out, buffer_4_out, det_1_out_2, In0);
  not not_1 (not_1_out, state_3_q);
  not not_2 (not_2_out, state_2_q);
  not not_3 (not_3_out, state_1_q);
  not not_4 (not_4_out, state_0_q);
  not not_5 (not_5_out, In_3);
  not not_6 (not_6_out, In_2);
  not not_7 (not_7_out, and_3_out);
  not not_8 (not_8_out, and_4_out);
  buf buffer_16 (buffer_16_out, buffer_15_out);
  buf buffer_17 (buffer_17_out, buffer_16_out);
  buf buffer_18 (buffer_18_out, buffer_17_out);
  and and_5 (and_5_out, not_1_out, state_2_q, state_0_q, buffer_15_out, In_3, In_2, and_3_out, and_4_out);
  and and_6 (and_6_out, not_1_out, state_2_q, state_1_q, state_0_q, buffer_15_out);
  and and_7 (and_7_out, state_3_q, not_2_out, not_3_out, buffer_15_out);
  and and_8 (and_8_out, state_3_q, not_2_out, state_1_q, state_0_q);
  or or_1 (or_1_out, state_2_q, state_1_q);
  or or_2 (or_2_out, state_2_q, state_0_q);
  or or_3 (or_3_out, state_1_q, not_4_out, not_5_out, not_6_out, not_7_out, not_8_out);
  or or_4 (or_4_out, not_2_out, not_3_out, not_4_out);
  and and_9 (and_9_out, not_1_out, not_3_out, state_0_q, buffer_15_out);
  and and_10 (and_10_out, not_2_out, not_3_out, state_0_q, buffer_15_out);
  and and_11 (and_11_out, not_1_out, state_1_q, not_4_out, buffer_15_out);
  and and_12 (and_12_out, state_3_q, not_2_out, state_1_q, state_0_q);
  and and_13 (and_13_out, not_1_out, not_4_out, buffer_15_out);
  and and_14 (and_14_out, not_2_out, not_4_out, buffer_15_out);
  and and_15 (and_15_out, not_1_out, state_2_q, not_3_out, buffer_15_out, In_3, In_2, and_3_out, and_4_out);
  and and_16 (and_16_out, state_3_q, not_2_out, state_1_q, state_0_q);
  or or_5 (or_5_out, and_5_out, and_6_out, and_7_out, and_8_out);
  and and_17 (and_17_out, or_1_out, or_2_out, buffer_15_out, or_3_out, or_4_out, not_1_out);
  or or_6 (or_6_out, and_9_out, and_10_out, and_11_out, and_12_out);
  or or_7 (or_7_out, and_13_out, and_14_out, and_15_out, and_16_out);
  buf buffer_19 (buffer_19_out, buffer_18_out);
  buf buffer_20 (buffer_20_out, buffer_19_out);
  buf buffer_21 (buffer_21_out, buffer_20_out);
  buf buffer_22 (buffer_22_out, buffer_21_out);
  D_Flip_Flop state_3 (.D(or_5_out), .clk(buffer_18_out), .Q(state_3_q));  // open: Qn, preset, reset
  D_Flip_Flop state_2 (.D(and_17_out), .clk(buffer_18_out), .Q(state_2_q));  // open: Qn, preset, reset
  D_Flip_Flop state_1 (.D(or_6_out), .clk(buffer_18_out), .Q(state_1_q));  // open: Qn, preset, reset
  D_Flip_Flop state_0 (.D(or_7_out), .clk(buffer_18_out), .Q(state_0_q));  // open: Qn, preset, reset
  buf buffer_23 (buffer_23_out, buffer_22_out);
  buf buffer_24 (buffer_24_out, buffer_23_out);
  and and_18 (and_18_out, buffer_24_out, clock, state_3_q);
  and and_19 (and_19_out, buffer_24_out, clock, state_2_q);
  and and_20 (and_20_out, buffer_24_out, clock, state_1_q);
  and and_21 (and_21_out, buffer_24_out, clock, state_0_q);
  combine combine_1 (
    .S3(and_18_out), .S2(and_19_out), .S1(and_20_out), .S0(and_21_out), .In3(In_3), .In2(In_2), .mode(mode),
    .MAR_R(MAR_R), .AR_MR_W(AR_MR_W), .IR_to_MBR(IR_to_MBR), .R0_R(R0_R), .MBR_R(MBR_R), .L_R_W(L_R_W),
    .RAM_to_DR(RAM_to_DR), .DR_W(DR_W), .re_to_Aout(re_to_Aout), .command(command), .REG_12_R(REG_12_R),
    .PC_R(PC_R), .MAR_W(MAR_W), .DR_R(DR_R), .MBR_W(MBR_W), .IR_W(IR_W), .PC_inc(PC_inc), .IR_R(IR_R),
    .Reg_to_RAM(Reg_to_RAM), .R0_W(R0_W), .Aout_R(Aout_R), .REG_12_W(REG_12_W), .D_W(D_W));
endmodule

module D_Register (
  input  Write_en,
  input  in_3,
  input  in_2,
  input  in_1,
  input  in_0,
  output out_3,
  output out_2,
  output out_1,
  output out_0
);

  wire and_1_out, and_2_out, and_3_out, and_4_out, buffer_1_out, buffer_2_out;

  and and_1 (and_1_out, in_3, Write_en);
  and and_2 (and_2_out, in_2, Write_en);
  and and_3 (and_3_out, in_1, Write_en);
  and and_4 (and_4_out, in_0, Write_en);
  buf buffer_1 (buffer_1_out, Write_en);
  buf buffer_2 (buffer_2_out, buffer_1_out);
  D_Flip_Flop store_3 (.D(and_1_out), .clk(buffer_2_out), .Q(out_3));  // open: Qn, preset, reset
  D_Flip_Flop store_2 (.D(and_2_out), .clk(buffer_2_out), .Q(out_2));  // open: Qn, preset, reset
  D_Flip_Flop store_1 (.D(and_3_out), .clk(buffer_2_out), .Q(out_1));  // open: Qn, preset, reset
  D_Flip_Flop store_0 (.D(and_4_out), .clk(buffer_2_out), .Q(out_0));  // open: Qn, preset, reset
  // Probe on out_2
  // Probe on out_3
  // Probe on out_1
  // Probe on out_0
endmodule

module LED_1 (
  input  In0,
  input  In1,
  input  In2,
  input  In3,
  output Out1,
  output Out2,
  output Out3,
  output Out4,
  output Out5,
  output Out6,
  output Out7,
  output Out_4_2,
  output Out_7_2
);

  wire and_1_out, and_2_out, and_3_out, and_4_out, and_5_out, and_6_out, and_7_out, and_8_out, and_9_out,
       and_10_out, and_11_out, and_12_out, and_13_out, and_14_out, and_15_out, and_16_out, and_17_out,
       and_18_out, and_19_out, and_20_out, and_21_out, not_1_out, not_2_out, not_3_out, not_4_out, or_1_out,
       or_2_out, or_3_out, or_4_out, or_5_out, or_6_out, or_7_out, or_8_out, or_9_out, or_10_out, or_11_out,
       or_12_out, or_13_out, or_14_out, or_15_out, or_16_out, or_17_out;

  not not_1 (not_1_out, In0);
  not not_2 (not_2_out, In1);
  not not_3 (not_3_out, In2);
  not not_4 (not_4_out, In3);
  or or_1 (or_1_out, In1, In2, In3);
  or or_2 (or_2_out, not_2_out, In2, not_4_out);
  or or_3 (or_3_out, not_1_out, not_2_out, not_3_out, In3);
  and and_1 (and_1_out, not_1_out, not_2_out, not_3_out);
  and and_2 (and_2_out, not_1_out, not_3_out, In3);
  and and_3 (and_3_out, not_2_out, not_3_out, In3);
  and and_4 (and_4_out, not_1_out, In2, not_4_out);
  and and_5 (and_5_out, not_2_out, In2, not_4_out);
  and and_6 (and_6_out, In1, In2, In3);
  or or_4 (or_4_out, In0, In1, not_3_out, In3);
  or or_5 (or_5_out, In0, not_2_out, not_3_out, not_4_out);
  or or_6 (or_6_out, not_1_out, In1, In2, In3);
  or or_7 (or_7_out, not_1_out, not_2_out, In2, not_4_out);
  or or_8 (or_8_out, In0, not_2_out, not_3_out, In3);
  or or_9 (or_9_out, not_1_out, In1, not_3_out, In3);
  or or_10 (or_10_out, not_1_out, not_2_out, not_3_out, not_4_out);
  and and_7 (and_7_out, not_1_out, not_3_out);
  and and_8 (and_8_out, not_1_out, not_2_out, In3);
  and and_9 (and_9_out, not_1_out, In1, not_4_out);
  or or_11 (or_11_out, In0, In1, not_3_out, In3);
  or or_12 (or_12_out, In0, not_2_out, not_3_out, not_4_out);
  or or_13 (or_13_out, not_1_out, In1, In2);
  or or_14 (or_14_out, not_1_out, In2, not_4_out);
  or or_15 (or_15_out, not_1_out, not_2_out, not_3_out, In3);
  or or_16 (or_16_out, In0, In1, not_3_out, not_4_out);
  or or_17 (or_17_out, In0, not_2_out, In2, In3);
  and and_10 (and_10_out, In3, not_3_out, In1, not_1_out);
  and and_11 (and_11_out, In3, not_3_out, In1, In0);
  and and_12 (and_12_out, In3, In2, not_2_out, not_1_out);
  and and_13 (and_13_out, In3, In2, not_2_out, In0);
  and and_14 (and_14_out, In3, In2, In1, not_1_out);
  and and_15 (and_15_out, In3, In2, In1, In0);
  and and_16 (and_16_out, In3, not_3_out, In1, not_1_out);
  and and_17 (and_17_out, In3, not_3_out, In1, In0);
  and and_18 (and_18_out, In3, In2, not_2_out, not_1_out);
  and and_19 (and_19_out, In3, In2, not_2_out, In0);
  and and_20 (and_20_out, In3, In2, In1, not_1_out);
  and and_21 (and_21_out, In3, In2, In1, In0);
  and and_22 (Out1, or_1_out, or_2_out, or_3_out);
  or or_18 (Out2, and_1_out, and_2_out, and_3_out, and_4_out, and_5_out, and_6_out);
  and and_23 (Out3, or_4_out, or_5_out, or_6_out, or_7_out);
  and and_24 (Out4, or_8_out, or_9_out, or_10_out);
  or or_19 (Out5, and_7_out, and_8_out, and_9_out);
  and and_25 (Out6, or_11_out, or_12_out, or_13_out, or_14_out, or_15_out);
  and and_26 (Out7, or_16_out, or_17_out);
  or or_20 (Out_4_2, and_10_out, and_11_out, and_12_out, and_13_out, and_14_out, and_15_out);
  or or_21 (Out_7_2, and_16_out, and_17_out, and_18_out, and_19_out, and_20_out, and_21_out);
endmodule

module R0_Register (
  input  Write_en,
  input  in_0,
  input  in_1,
  input  in_2,
  input  in_3,
  input  Read_en,
  input  R0_R_en,
  output out_0,
  output out_1,
  output out_2,
  output out_3,
  output read_0,
  output read_1,
  output read_2,
  output read_3
);

  wire and_1_out, and_2_out, and_3_out, and_4_out, buffer_1_out, buffer_2_out, store_0_q, store_1_q,
       store_2_q, store_3_q;

  and and_1 (and_1_out, in_0, Write_en);
  and and_2 (and_2_out, in_1, Write_en);
  and and_3 (and_3_out, in_2, Write_en);
  and and_4 (and_4_out, in_3, Write_en);
  buf buffer_1 (buffer_1_out, Write_en);
  buf buffer_2 (buffer_2_out, buffer_1_out);
  D_Flip_Flop store_0 (.D(and_1_out), .clk(buffer_2_out), .Q(store_0_q));  // open: Qn, preset, reset
  D_Flip_Flop store_1 (.D(and_2_out), .clk(buffer_2_out), .Q(store_1_q));  // open: Qn, preset, reset
  D_Flip_Flop store_2 (.D(and_3_out), .clk(buffer_2_out), .Q(store_2_q));  // open: Qn, preset, reset
  D_Flip_Flop store_3 (.D(and_4_out), .clk(buffer_2_out), .Q(store_3_q));  // open: Qn, preset, reset
  // Probe on store_2_q
  // Probe on store_3_q
  // Probe on store_1_q
  // Probe on store_0_q
  and and_5 (out_0, store_0_q, Read_en);
  and and_6 (out_1, store_1_q, Read_en);
  and and_7 (out_2, store_2_q, Read_en);
  and and_8 (out_3, store_3_q, Read_en);
  and and_9 (read_0, store_0_q, R0_R_en);
  and and_10 (read_1, store_1_q, R0_R_en);
  and and_11 (read_2, store_2_q, R0_R_en);
  and and_12 (read_3, store_3_q, R0_R_en);

  // Notes on the sheet:
  //   current stored 4-bit data
endmodule

module my_buffer (
  input  in_1,
  output out_2
);

  wire buffer_1_out, buffer_2_out, buffer_3_out, buffer_4_out, buffer_5_out, buffer_6_out, buffer_7_out,
       buffer_8_out, buffer_9_out, buffer_10_out, buffer_11_out, buffer_12_out, buffer_13_out, buffer_14_out,
       buffer_15_out, buffer_16_out, buffer_17_out, buffer_18_out;

  buf buffer_1 (buffer_1_out, in_1);
  buf buffer_2 (buffer_2_out, buffer_1_out);
  buf buffer_3 (buffer_3_out, buffer_2_out);
  buf buffer_4 (buffer_4_out, buffer_3_out);
  buf buffer_5 (buffer_5_out, buffer_4_out);
  buf buffer_6 (buffer_6_out, buffer_5_out);
  buf buffer_7 (buffer_7_out, buffer_6_out);
  buf buffer_8 (buffer_8_out, buffer_7_out);
  buf buffer_9 (buffer_9_out, buffer_8_out);
  buf buffer_10 (buffer_10_out, buffer_9_out);
  buf buffer_11 (buffer_11_out, buffer_10_out);
  buf buffer_12 (buffer_12_out, buffer_11_out);
  buf buffer_13 (buffer_13_out, buffer_12_out);
  buf buffer_14 (buffer_14_out, buffer_13_out);
  buf buffer_15 (buffer_15_out, buffer_14_out);
  buf buffer_16 (buffer_16_out, buffer_15_out);
  buf buffer_17 (buffer_17_out, buffer_16_out);
  buf buffer_18 (buffer_18_out, buffer_17_out);
  buf buffer_19 (out_2, buffer_18_out);
endmodule
