// Logisim project a5 (2).circ as structural Verilog: 6 circuits, main circuit main
module main (
  input  d3,
  input  d2,
  input  d1,
  input  d0,
  input  Mode,
  input  a2,
  input  a1,
  input  a0,
  output out3,
  output out2,
  output out1,
  output out0
);

  wire address_register_1_output_bit_0, address_register_1_output_bit_1, address_register_1_output_bit_2,
       address_register_1_status, and_1_out, and_2_out, and_3_out, and_4_out, and_5_out, and_6_out,
       and_7_out, and_8_out, and_9_out, and_10_out, and_11_out, and_12_out, and_13_out, and_14_out,
       and_15_out, and_16_out, and_17_out, and_18_out, and_19_out, and_20_out, and_21_out, and_22_out,
       and_23_out, and_24_out, and_25_out, and_26_out, and_27_out, and_28_out, and_29_out, and_30_out,
       and_31_out, and_32_out, and_33_out, and_34_out, and_35_out, and_36_out, and_37_out, and_38_out,
       and_39_out, and_40_out, and_41_out, and_42_out, and_43_out, and_44_out, and_45_out, and_46_out,
       and_47_out, and_48_out, and_49_out, buffer_1_out, buffer_2_out, buffer_3_out, buffer_4_out,
       buffer_5_out, buffer_6_out, buffer_7_out, buffer_8_out, input_register_1_output_bit_0,
       input_register_1_output_bit_1, input_register_1_output_bit_2, input_register_1_output_bit_3,
       mode_register_1_mode_bit_out, nibble_1_output_bit_0, nibble_1_output_bit_1, nibble_1_output_bit_2,
       nibble_1_output_bit_3, nibble_2_output_bit_0, nibble_2_output_bit_1, nibble_2_output_bit_2,
       nibble_2_output_bit_3, nibble_3_output_bit_0, nibble_3_output_bit_1, nibble_3_output_bit_2,
       nibble_3_output_bit_3, nibble_4_output_bit_0, nibble_4_output_bit_1, nibble_4_output_bit_2,
       nibble_4_output_bit_3, nibble_5_output_bit_0, nibble_5_output_bit_1, nibble_5_output_bit_2,
       nibble_5_output_bit_3, nibble_6_output_bit_0, nibble_6_output_bit_1, nibble_6_output_bit_2,
       nibble_6_output_bit_3, nibble_7_output_bit_0, nibble_7_output_bit_1, nibble_7_output_bit_2,
       nibble_7_output_bit_3, nibble_8_output_bit_0, nibble_8_output_bit_1, nibble_8_output_bit_2,
       nibble_8_output_bit_3, or_1_out, or_2_out, or_3_out, or_4_out, or_5_out, or_6_out, or_7_out, or_8_out,
       or_9_out, or_10_out, or_11_out, or_12_out, or_13_out, or_14_out, or_15_out, or_16_out, or_17_out,
       or_18_out, or_19_out, or_20_out, or_21_out, or_22_out, or_23_out, or_24_out, or_25_out, or_26_out,
       or_27_out, or_28_out, Ram_Clock_out;

  address_register address_register_1 (
    .output_bit_0(address_register_1_output_bit_0), .output_bit_1(address_register_1_output_bit_1),
    .output_bit_2(address_register_1_output_bit_2), .status(address_register_1_status),
    .Activate(Ram_Clock_out), .Data_bit_0(a0), .Data_bit_1(a1), .Data_bit_2(a2));
  Clock Ram_Clock (.out(Ram_Clock_out));
  mode_register mode_register_1 (
    .mode_bit_out(mode_register_1_mode_bit_out), .Activate(Ram_Clock_out), .mode_bit(Mode));
  and and_1 (and_1_out, ~address_register_1_output_bit_0, ~address_register_1_output_bit_1, ~address_register_1_output_bit_2, Ram_Clock_out, ~mode_register_1_mode_bit_out, address_register_1_status);  // AND_Gate
  and and_2 (and_2_out, address_register_1_output_bit_0, ~address_register_1_output_bit_1, ~address_register_1_output_bit_2, Ram_Clock_out, ~mode_register_1_mode_bit_out);  // AND_Gate
  and and_3 (and_3_out, ~address_register_1_output_bit_0, address_register_1_output_bit_1, ~address_register_1_output_bit_2, Ram_Clock_out, ~mode_register_1_mode_bit_out);  // AND_Gate
  and and_4 (and_4_out, address_register_1_output_bit_0, address_register_1_output_bit_1, ~address_register_1_output_bit_2, Ram_Clock_out, ~mode_register_1_mode_bit_out);  // AND_Gate
  and and_5 (and_5_out, ~address_register_1_output_bit_0, ~address_register_1_output_bit_1, address_register_1_output_bit_2, Ram_Clock_out, ~mode_register_1_mode_bit_out);  // AND_Gate
  and and_6 (and_6_out, address_register_1_output_bit_0, ~address_register_1_output_bit_1, address_register_1_output_bit_2, Ram_Clock_out, ~mode_register_1_mode_bit_out);  // AND_Gate
  and and_7 (and_7_out, ~address_register_1_output_bit_0, address_register_1_output_bit_1, address_register_1_output_bit_2, Ram_Clock_out, ~mode_register_1_mode_bit_out);  // AND_Gate
  and and_8 (and_8_out, address_register_1_output_bit_0, address_register_1_output_bit_1, address_register_1_output_bit_2, Ram_Clock_out, ~mode_register_1_mode_bit_out);  // AND_Gate
  input_register input_register_1 (
    .output_bit_0(input_register_1_output_bit_0), .output_bit_1(input_register_1_output_bit_1),
    .output_bit_2(input_register_1_output_bit_2), .output_bit_3(input_register_1_output_bit_3),
    .Activate(Ram_Clock_out), .Data_bit_0(d0), .Data_bit_1(d1), .Data_bit_2(d2), .Data_bit_3(d3));
  buf buffer_1 (buffer_1_out, address_register_1_status);
  buf buffer_2 (buffer_2_out, buffer_1_out);
  buf buffer_3 (buffer_3_out, buffer_2_out);
  buf buffer_4 (buffer_4_out, buffer_3_out);
  buf buffer_5 (buffer_5_out, buffer_4_out);
  buf buffer_6 (buffer_6_out, buffer_5_out);
  buf buffer_7 (buffer_7_out, buffer_6_out);
  buf buffer_8 (buffer_8_out, buffer_7_out);
  Nibble nibble_1 (
    .output_bit_0(nibble_1_output_bit_0), .output_bit_1(nibble_1_output_bit_1),
    .output_bit_2(nibble_1_output_bit_2), .output_bit_3(nibble_1_output_bit_3), .Activate(and_1_out),
    .Data_bit_0(input_register_1_output_bit_0), .Data_bit_1(input_register_1_output_bit_1),
    .Data_bit_2(input_register_1_output_bit_2), .Data_bit_3(input_register_1_output_bit_3));
  Nibble nibble_2 (
    .output_bit_0(nibble_2_output_bit_0), .output_bit_1(nibble_2_output_bit_1),
    .output_bit_2(nibble_2_output_bit_2), .output_bit_3(nibble_2_output_bit_3), .Activate(and_2_out),
    .Data_bit_0(input_register_1_output_bit_0), .Data_bit_1(input_register_1_output_bit_1),
    .Data_bit_2(input_register_1_output_bit_2), .Data_bit_3(input_register_1_output_bit_3));
  Nibble nibble_3 (
    .output_bit_0(nibble_3_output_bit_0), .output_bit_1(nibble_3_output_bit_1),
    .output_bit_2(nibble_3_output_bit_2), .output_bit_3(nibble_3_output_bit_3), .Activate(and_3_out),
    .Data_bit_0(input_register_1_output_bit_0), .Data_bit_1(input_register_1_output_bit_1),
    .Data_bit_2(input_register_1_output_bit_2), .Data_bit_3(input_register_1_output_bit_3));
  Nibble nibble_4 (
    .output_bit_0(nibble_4_output_bit_0), .output_bit_1(nibble_4_output_bit_1),
    .output_bit_2(nibble_4_output_bit_2), .output_bit_3(nibble_4_output_bit_3), .Activate(and_4_out),
    .Data_bit_0(input_register_1_output_bit_0), .Data_bit_1(input_register_1_output_bit_1),
    .Data_bit_2(input_register_1_output_bit_2), .Data_bit_3(input_register_1_output_bit_3));
  Nibble nibble_5 (
    .output_bit_0(nibble_5_output_bit_0), .output_bit_1(nibble_5_output_bit_1),
    .output_bit_2(nibble_5_output_bit_2), .output_bit_3(nibble_5_output_bit_3), .Activate(and_5_out),
    .Data_bit_0(input_register_1_output_bit_0), .Data_bit_1(input_register_1_output_bit_1),
    .Data_bit_2(input_register_1_output_bit_2), .Data_bit_3(input_register_1_output_bit_3));
  Nibble nibble_6 (
    .output_bit_0(nibble_6_output_bit_0), .output_bit_1(nibble_6_output_bit_1),
    .output_bit_2(nibble_6_output_bit_2), .output_bit_3(nibble_6_output_bit_3), .Activate(and_6_out),
    .Data_bit_0(input_register_1_output_bit_0), .Data_bit_1(input_register_1_output_bit_1),
    .Data_bit_2(input_register_1_output_bit_2), .Data_bit_3(input_register_1_output_bit_3));
  Nibble nibble_7 (
    .output_bit_0(nibble_7_output_bit_0), .output_bit_1(nibble_7_output_bit_1),
    .output_bit_2(nibble_7_output_bit_2), .output_bit_3(nibble_7_output_bit_3), .Activate(and_7_out),
    .Data_bit_0(input_register_1_output_bit_0), .Data_bit_1(input_register_1_output_bit_1),
    .Data_bit_2(input_register_1_output_bit_2), .Data_bit_3(input_register_1_output_bit_3));
  Nibble nibble_8 (
    .output_bit_0(nibble_8_output_bit_0), .output_bit_1(nibble_8_output_bit_1),
    .output_bit_2(nibble_8_output_bit_2), .output_bit_3(nibble_8_output_bit_3), .Activate(and_8_out),
    .Data_bit_0(input_register_1_output_bit_0), .Data_bit_1(input_register_1_output_bit_1),
    .Data_bit_2(input_register_1_output_bit_2), .Data_bit_3(input_register_1_output_bit_3));
  and and_9 (and_9_out, Ram_Clock_out, buffer_8_out);
  and and_10 (and_10_out, ~address_register_1_output_bit_2, ~address_register_1_output_bit_1, ~address_register_1_output_bit_0);  // AND_Gate
  and and_11 (and_11_out, ~address_register_1_output_bit_2, ~address_register_1_output_bit_1, address_register_1_output_bit_0);  // AND_Gate
  and and_12 (and_12_out, ~address_register_1_output_bit_2, address_register_1_output_bit_1, ~address_register_1_output_bit_0);  // AND_Gate
  output_register output_register_1 (
    .output_bit_0(out0), .output_bit_1(out1), .output_bit_2(out2), .output_bit_3(out3), .Activate(and_9_out),
    .Data_bit_0(or_22_out), .Data_bit_1(or_15_out), .Data_bit_2(or_8_out), .Data_bit_3(or_1_out));
  and and_13 (and_13_out, ~address_register_1_output_bit_2, address_register_1_output_bit_1, address_register_1_output_bit_0);  // AND_Gate
  and and_14 (and_14_out, address_register_1_output_bit_2, ~address_register_1_output_bit_1, ~address_register_1_output_bit_0);  // AND_Gate
  and and_15 (and_15_out, address_register_1_output_bit_2, ~address_register_1_output_bit_1, address_register_1_output_bit_0);  // AND_Gate
  and and_16 (and_16_out, address_register_1_output_bit_2, address_register_1_output_bit_1, ~address_register_1_output_bit_0);  // AND_Gate
  and and_17 (and_17_out, address_register_1_output_bit_2, address_register_1_output_bit_1, address_register_1_output_bit_0);
  and and_18 (and_18_out, nibble_1_output_bit_0, Ram_Clock_out, mode_register_1_mode_bit_out, and_10_out);
  and and_19 (and_19_out, nibble_2_output_bit_0, Ram_Clock_out, mode_register_1_mode_bit_out, and_11_out);
  and and_20 (and_20_out, nibble_3_output_bit_0, Ram_Clock_out, mode_register_1_mode_bit_out, and_12_out);
  and and_21 (and_21_out, nibble_4_output_bit_0, Ram_Clock_out, mode_register_1_mode_bit_out, and_13_out);
  and and_22 (and_22_out, nibble_5_output_bit_0, Ram_Clock_out, mode_register_1_mode_bit_out, and_14_out);
  and and_23 (and_23_out, nibble_6_output_bit_0, Ram_Clock_out, mode_register_1_mode_bit_out, and_15_out);
  and and_24 (and_24_out, nibble_7_output_bit_0, Ram_Clock_out, mode_register_1_mode_bit_out, and_16_out);
  and and_25 (and_25_out, nibble_8_output_bit_0, Ram_Clock_out, mode_register_1_mode_bit_out, and_17_out);
  and and_26 (and_26_out, nibble_1_output_bit_1, Ram_Clock_out, mode_register_1_mode_bit_out, and_10_out);
  and and_27 (and_27_out, nibble_1_output_bit_2, Ram_Clock_out, mode_register_1_mode_bit_out, and_10_out);
  and and_28 (and_28_out, nibble_2_output_bit_1, Ram_Clock_out, mode_register_1_mode_bit_out, and_11_out);
  and and_29 (and_29_out, nibble_2_output_bit_2, Ram_Clock_out, mode_register_1_mode_bit_out, and_11_out);
  and and_30 (and_30_out, nibble_3_output_bit_1, Ram_Clock_out, mode_register_1_mode_bit_out, and_12_out);
  and and_31 (and_31_out, nibble_3_output_bit_2, Ram_Clock_out, mode_register_1_mode_bit_out, and_12_out);
  and and_32 (and_32_out, nibble_4_output_bit_1, Ram_Clock_out, mode_register_1_mode_bit_out, and_13_out);
  and and_33 (and_33_out, nibble_4_output_bit_2, Ram_Clock_out, mode_register_1_mode_bit_out, and_13_out);
  and and_34 (and_34_out, nibble_5_output_bit_1, Ram_Clock_out, mode_register_1_mode_bit_out, and_14_out);
  and and_35 (and_35_out, nibble_5_output_bit_2, Ram_Clock_out, mode_register_1_mode_bit_out, and_14_out);
  and and_36 (and_36_out, nibble_6_output_bit_1, Ram_Clock_out, mode_register_1_mode_bit_out, and_15_out);
  and and_37 (and_37_out, nibble_6_output_bit_2, Ram_Clock_out, mode_register_1_mode_bit_out, and_15_out);
  and and_38 (and_38_out, nibble_7_output_bit_1, Ram_Clock_out, mode_register_1_mode_bit_out, and_16_out);
  and and_39 (and_39_out, nibble_7_output_bit_2, Ram_Clock_out, mode_register_1_mode_bit_out, and_16_out);
  and and_40 (and_40_out, nibble_8_output_bit_1, Ram_Clock_out, mode_register_1_mode_bit_out, and_17_out);
  and and_41 (and_41_out, nibble_8_output_bit_2, Ram_Clock_out, mode_register_1_mode_bit_out, and_17_out);
  and and_42 (and_42_out, nibble_1_output_bit_3, Ram_Clock_out, mode_register_1_mode_bit_out, and_10_out);
  and and_43 (and_43_out, nibble_2_output_bit_3, Ram_Clock_out, mode_register_1_mode_bit_out, and_11_out);
  and and_44 (and_44_out, nibble_3_output_bit_3, Ram_Clock_out, mode_register_1_mode_bit_out, and_12_out);
  and and_45 (and_45_out, nibble_4_output_bit_3, Ram_Clock_out, mode_register_1_mode_bit_out, and_13_out);
  and and_46 (and_46_out, nibble_5_output_bit_3, Ram_Clock_out, mode_register_1_mode_bit_out, and_14_out);
  and and_47 (and_47_out, nibble_6_output_bit_3, Ram_Clock_out, mode_register_1_mode_bit_out, and_15_out);
  and and_48 (and_48_out, nibble_7_output_bit_3, Ram_Clock_out, mode_register_1_mode_bit_out, and_16_out);
  and and_49 (and_49_out, nibble_8_output_bit_3, Ram_Clock_out, mode_register_1_mode_bit_out, and_17_out);
  or or_1 (or_1_out, or_2_out, and_42_out);
  or or_2 (or_2_out, or_3_out, and_43_out);
  or or_3 (or_3_out, or_4_out, and_44_out);
  or or_4 (or_4_out, or_5_out, and_45_out);
  or or_5 (or_5_out, or_6_out, and_46_out);
  or or_6 (or_6_out, or_7_out, and_47_out);
  or or_7 (or_7_out, and_49_out, and_48_out);
  or or_8 (or_8_out, or_9_out, and_27_out);
  or or_9 (or_9_out, or_10_out, and_29_out);
  or or_10 (or_10_out, or_11_out, and_31_out);
  or or_11 (or_11_out, or_12_out, and_33_out);
  or or_12 (or_12_out, or_13_out, and_35_out);
  or or_13 (or_13_out, or_14_out, and_37_out);
  or or_14 (or_14_out, and_41_out, and_39_out);
  or or_15 (or_15_out, or_16_out, and_26_out);
  or or_16 (or_16_out, or_17_out, and_28_out);
  or or_17 (or_17_out, or_18_out, and_30_out);
  or or_18 (or_18_out, or_19_out, and_32_out);
  or or_19 (or_19_out, or_20_out, and_34_out);
  or or_20 (or_20_out, or_21_out, and_36_out);
  or or_21 (or_21_out, and_40_out, and_38_out);
  or or_22 (or_22_out, or_23_out, and_18_out);
  or or_23 (or_23_out, or_24_out, and_19_out);
  or or_24 (or_24_out, or_25_out, and_20_out);
  or or_25 (or_25_out, or_26_out, and_21_out);
  or or_26 (or_26_out, or_27_out, and_22_out);
  or or_27 (or_27_out, or_28_out, and_23_out);
  or or_28 (or_28_out, and_25_out, and_24_out);

  // Notes on the sheet:
  //   3-bit address input pins
  //   Jiahang Wang   ID:261011319
  //   Mode_Input_pin
  //   4-bit data input pins
  //   clock
  //   a0
  //   a1
  //   mode
  //   a2
  //   0
  //   1
  //   2
  //   3
  //   4
  //   5
  //   6
  //   7
  //   clock
  //   0
  //   0
  //   1
  //   1
  //   2
  //   2
  //   3
  //   3
  //   4
  //   4
  //   5
  //   5
  //   6
  //   6
  //   4-bit data output pins
  //   7
  //   7
  //   0ut_3
  //   0ut_2
  //   0ut_1
  //   0ut_0
endmodule

module Nibble (
  input  Data_bit_0,
  input  Data_bit_1,
  input  Data_bit_2,
  input  Data_bit_3,
  input  Activate,
  output output_bit_0,
  output output_bit_1,
  output output_bit_2,
  output output_bit_3
);

  D_Flip_Flop store_bit_0 (.D(Data_bit_0), .clk(Activate), .Q(output_bit_0));  // open: Qn, preset, reset
  D_Flip_Flop store_bit_1 (.D(Data_bit_1), .clk(Activate), .Q(output_bit_1));  // open: Qn, preset, reset
  D_Flip_Flop store_bit_2 (.D(Data_bit_2), .clk(Activate), .Q(output_bit_2));  // open: Qn, preset, reset
  D_Flip_Flop store_bit_3 (.D(Data_bit_3), .clk(Activate), .Q(output_bit_3));  // open: Qn, preset, reset
endmodule

module mode_register (
  input  mode_bit,
  input  Activate,
  output mode_bit_out
);

  wire d_ff_1_q, d_ff_1_qn, d_ff_2_q, not_1_out, store_mode_q;

  D_Flip_Flop store_mode (.D(mode_bit), .clk(Activate), .Q(store_mode_q));  // open: Qn, preset, reset
  D_Flip_Flop d_ff_1 (.D(d_ff_1_qn), .clk(Activate), .Q(d_ff_1_q), .Qn(d_ff_1_qn));  // open: preset, reset
  D_Flip_Flop d_ff_2 (.D(d_ff_1_q), .clk(not_1_out), .Q(d_ff_2_q));  // open: Qn, preset, reset
  not not_1 (not_1_out, Activate);
  and and_1 (mode_bit_out, store_mode_q, Activate, d_ff_2_q);
endmodule

module input_register (
  input  Data_bit_0,
  input  Data_bit_1,
  input  Data_bit_2,
  input  Data_bit_3,
  input  Activate,
  output output_bit_0,
  output output_bit_1,
  output output_bit_2,
  output output_bit_3
);

  wire d_ff_1_q, d_ff_1_qn, d_ff_2_q, input_store_0_q, input_store_1_q, input_store_2_q, input_store_3_q,
       not_1_out;

  D_Flip_Flop input_store_0 (.D(Data_bit_0), .clk(Activate), .Q(input_store_0_q));  // open: Qn, preset, reset
  D_Flip_Flop input_store_1 (.D(Data_bit_1), .clk(Activate), .Q(input_store_1_q));  // open: Qn, preset, reset
  D_Flip_Flop input_store_2 (.D(Data_bit_2), .clk(Activate), .Q(input_store_2_q));  // open: Qn, preset, reset
  D_Flip_Flop input_store_3 (.D(Data_bit_3), .clk(Activate), .Q(input_store_3_q));  // open: Qn, preset, reset
  D_Flip_Flop d_ff_1 (.D(d_ff_1_qn), .clk(Activate), .Q(d_ff_1_q), .Qn(d_ff_1_qn));  // open: preset, reset
  D_Flip_Flop d_ff_2 (.D(d_ff_1_q), .clk(not_1_out), .Q(d_ff_2_q));  // open: Qn, preset, reset
  not not_1 (not_1_out, Activate);
  and and_1 (output_bit_0, input_store_0_q, Activate, d_ff_2_q);
  and and_2 (output_bit_1, input_store_1_q, Activate, d_ff_2_q);
  and and_3 (output_bit_2, input_store_2_q, Activate, d_ff_2_q);
  and and_4 (output_bit_3, input_store_3_q, Activate, d_ff_2_q);
endmodule

module address_register (
  input  Data_bit_0,
  input  Data_bit_1,
  input  Data_bit_2,
  input  Activate,
  output output_bit_0,
  output output_bit_1,
  output output_bit_2,
  output status
);

  wire address_store_0_q, address_store_1_q, address_store_2_q, d_ff_1_q, d_ff_1_qn, d_ff_2_q, not_1_out;

  D_Flip_Flop address_store_0 (.D(Data_bit_0), .clk(Activate), .Q(address_store_0_q));  // open: Qn, preset, reset
  D_Flip_Flop address_store_1 (.D(Data_bit_1), .clk(Activate), .Q(address_store_1_q));  // open: Qn, preset, reset
  D_Flip_Flop address_store_2 (.D(Data_bit_2), .clk(Activate), .Q(address_store_2_q));  // open: Qn, preset, reset
  D_Flip_Flop d_ff_1 (.D(d_ff_1_qn), .clk(Activate), .Q(d_ff_1_q), .Qn(d_ff_1_qn));  // open: preset, reset
  D_Flip_Flop d_ff_2 (.D(d_ff_1_q), .clk(not_1_out), .Q(d_ff_2_q));  // open: Qn, preset, reset
  not not_1 (not_1_out, Activate);
  and and_1 (output_bit_0, address_store_0_q, Activate, d_ff_2_q);
  and and_2 (output_bit_1, address_store_1_q, Activate, d_ff_2_q);
  and and_3 (output_bit_2, address_store_2_q, Activate, d_ff_2_q);
  and and_4 (status, d_ff_2_q, Activate);
endmodule

module output_register (
  input  Data_bit_0,
  input  Data_bit_1,
  input  Data_bit_2,
  input  Data_bit_3,
  input  Activate,
  output output_bit_0,
  output output_bit_1,
  output output_bit_2,
  output output_bit_3
);

  D_Flip_Flop output_store_0 (.D(Data_bit_0), .clk(Activate), .Q(output_bit_0));  // open: Qn, preset, reset
  D_Flip_Flop output_store_1 (.D(Data_bit_1), .clk(Activate), .Q(output_bit_1));  // open: Qn, preset, reset
  D_Flip_Flop output_store_2 (.D(Data_bit_2), .clk(Activate), .Q(output_bit_2));  // open: Qn, preset, reset
  D_Flip_Flop output_store_3 (.D(Data_bit_3), .clk(Activate), .Q(output_bit_3));  // open: Qn, preset, reset
endmodule
