// Logisim project mini5.circ as structural Verilog: 6 circuits, main circuit main
module main (
  input  d3,
  input  d2,
  input  d1,
  input  d0,
  input  Mode,
  input  a2,
  input  a1,
  input  a0,
  output o3,
  output o2,
  output o1,
  output o0
);

  wire address_register_1_output_bit_0, address_register_1_output_bit_1, address_register_1_output_bit_2,
       and_1_out, and_2_out, and_3_out, and_4_out, and_5_out, and_6_out, and_7_out, and_8_out, and_9_out,
       and_10_out, and_11_out, and_12_out, and_13_out, and_14_out, and_15_out, and_16_out, and_19_out,
       and_21_out, and_23_out, and_24_out, and_25_out, and_26_out, and_27_out, and_28_out, and_29_out,
       and_30_out, and_31_out, and_32_out, and_33_out, and_34_out, and_35_out, and_36_out, and_37_out,
       and_38_out, and_39_out, and_40_out, and_41_out, and_42_out, and_43_out, and_44_out, and_45_out,
       and_46_out, and_47_out, and_48_out, and_49_out, and_50_out, and_51_out, and_52_out, and_53_out,
       and_54_out, and_55_out, and_56_out, and_57_out, and_58_out, and_59_out, and_60_out,
       input_output_register_1_output_bit_0, input_output_register_1_output_bit_1,
       input_output_register_1_output_bit_2, input_output_register_1_output_bit_3,
       input_output_register_1_status_out, mode_register_1_output_mode_bit, nibble_1_output_bit_0,
       nibble_1_output_bit_1, nibble_1_output_bit_2, nibble_1_output_bit_3, nibble_2_output_bit_0,
       nibble_2_output_bit_1, nibble_2_output_bit_2, nibble_2_output_bit_3, nibble_3_output_bit_0,
       nibble_3_output_bit_1, nibble_3_output_bit_2, nibble_3_output_bit_3, nibble_4_output_bit_0,
       nibble_4_output_bit_1, nibble_4_output_bit_2, nibble_4_output_bit_3, nibble_5_output_bit_0,
       nibble_5_output_bit_1, nibble_5_output_bit_2, nibble_5_output_bit_3, nibble_6_output_bit_0,
       nibble_6_output_bit_1, nibble_6_output_bit_2, nibble_6_output_bit_3, nibble_7_output_bit_0,
       nibble_7_output_bit_1, nibble_7_output_bit_2, nibble_7_output_bit_3, nibble_8_output_bit_0,
       nibble_8_output_bit_1, nibble_8_output_bit_2, nibble_8_output_bit_3, or_1_out, or_2_out, or_3_out,
       or_4_out, or_5_out, or_6_out, or_7_out, or_8_out, or_9_out, or_10_out, or_11_out, or_12_out,
       or_13_out, or_14_out, or_15_out, or_16_out, or_17_out, or_18_out, or_19_out, or_20_out, or_21_out,
       or_22_out, or_23_out, or_24_out, or_25_out, or_26_out, or_27_out, or_28_out, or_29_out, or_30_out,
       or_31_out, or_32_out, Ram_Clock_out;

  Clock Ram_Clock (.out(Ram_Clock_out));
  address_register address_register_1 (
    .output_bit_0(address_register_1_output_bit_0), .output_bit_1(address_register_1_output_bit_1),
    .output_bit_2(address_register_1_output_bit_2), .Activate(Ram_Clock_out), .Data_bit_0(a0),
    .Data_bit_1(a1), .Data_bit_2(a2));  // open: s_bit_0, s_bit_1, s_bit_2
  mode_register mode_register_1 (
    .output_mode_bit(mode_register_1_output_mode_bit), .activate(Ram_Clock_out), .input_mode_bit(Mode));  // open: pre_mode_bit
  and and_1 (and_1_out, ~address_register_1_output_bit_0, ~address_register_1_output_bit_1, ~address_register_1_output_bit_2, Ram_Clock_out, ~mode_register_1_output_mode_bit);  // AND_Gate
  and and_2 (and_2_out, address_register_1_output_bit_0, ~address_register_1_output_bit_1, ~address_register_1_output_bit_2, Ram_Clock_out, ~mode_register_1_output_mode_bit);  // AND_Gate
  and and_3 (and_3_out, ~address_register_1_output_bit_0, address_register_1_output_bit_1, ~address_register_1_output_bit_2, Ram_Clock_out, ~mode_register_1_output_mode_bit);  // AND_Gate
  and and_4 (and_4_out, address_register_1_output_bit_0, address_register_1_output_bit_1, ~address_register_1_output_bit_2, Ram_Clock_out, ~mode_register_1_output_mode_bit);  // AND_Gate
  and and_5 (and_5_out, ~address_register_1_output_bit_0, ~address_register_1_output_bit_1, address_register_1_output_bit_2, Ram_Clock_out, ~mode_register_1_output_mode_bit);  // AND_Gate
  and and_6 (and_6_out, address_register_1_output_bit_0, ~address_register_1_output_bit_1, address_register_1_output_bit_2, Ram_Clock_out, ~mode_register_1_output_mode_bit);  // AND_Gate
  and and_7 (and_7_out, ~address_register_1_output_bit_0, address_register_1_output_bit_1, address_register_1_output_bit_2, Ram_Clock_out, ~mode_register_1_output_mode_bit);  // AND_Gate
  and and_8 (and_8_out, address_register_1_output_bit_0, address_register_1_output_bit_1, address_register_1_output_bit_2, Ram_Clock_out, ~mode_register_1_output_mode_bit);  // AND_Gate
  and and_9 (and_9_out, d0, ~mode_register_1_output_mode_bit);  // AND_Gate
  and and_10 (and_10_out, d1, ~mode_register_1_output_mode_bit);  // AND_Gate
  and and_11 (and_11_out, d2, ~mode_register_1_output_mode_bit);  // AND_Gate
  and and_12 (and_12_out, d3, ~mode_register_1_output_mode_bit);  // AND_Gate
  or or_1 (or_1_out, and_9_out, and_13_out);
  or or_2 (or_2_out, and_10_out, and_14_out);
  or or_3 (or_3_out, and_11_out, and_15_out);
  or or_4 (or_4_out, and_12_out, and_16_out);
  and and_13 (and_13_out, mode_register_1_output_mode_bit, or_26_out);
  and and_14 (and_14_out, mode_register_1_output_mode_bit, or_19_out);
  and and_15 (and_15_out, mode_register_1_output_mode_bit, or_12_out);
  and and_16 (and_16_out, or_5_out, mode_register_1_output_mode_bit);
  Nibble nibble_1 (
    .output_bit_0(nibble_1_output_bit_0), .output_bit_1(nibble_1_output_bit_1),
    .output_bit_2(nibble_1_output_bit_2), .output_bit_3(nibble_1_output_bit_3), .Activate(and_1_out),
    .Data_bit_0(input_output_register_1_output_bit_0), .Data_bit_1(input_output_register_1_output_bit_1),
    .Data_bit_2(input_output_register_1_output_bit_2), .Data_bit_3(input_output_register_1_output_bit_3));
  Nibble nibble_2 (
    .output_bit_0(nibble_2_output_bit_0), .output_bit_1(nibble_2_output_bit_1),
    .output_bit_2(nibble_2_output_bit_2), .output_bit_3(nibble_2_output_bit_3), .Activate(and_2_out),
    .Data_bit_0(input_output_register_1_output_bit_0), .Data_bit_1(input_output_register_1_output_bit_1),
    .Data_bit_2(input_output_register_1_output_bit_2), .Data_bit_3(input_output_register_1_output_bit_3));
  Nibble nibble_3 (
    .output_bit_0(nibble_3_output_bit_0), .output_bit_1(nibble_3_output_bit_1),
    .output_bit_2(nibble_3_output_bit_2), .output_bit_3(nibble_3_output_bit_3), .Activate(and_3_out),
    .Data_bit_0(input_output_register_1_output_bit_0), .Data_bit_1(input_output_register_1_output_bit_1),
    .Data_bit_2(input_output_register_1_output_bit_2), .Data_bit_3(input_output_register_1_output_bit_3));
  Nibble nibble_4 (
    .output_bit_0(nibble_4_output_bit_0), .output_bit_1(nibble_4_output_bit_1),
    .output_bit_2(nibble_4_output_bit_2), .output_bit_3(nibble_4_output_bit_3), .Activate(and_4_out),
    .Data_bit_0(input_output_register_1_output_bit_0), .Data_bit_1(input_output_register_1_output_bit_1),
    .Data_bit_2(input_output_register_1_output_bit_2), .Data_bit_3(input_output_register_1_output_bit_3));
  Nibble nibble_5 (
    .output_bit_0(nibble_5_output_bit_0), .output_bit_1(nibble_5_output_bit_1),
    .output_bit_2(nibble_5_output_bit_2), .output_bit_3(nibble_5_output_bit_3), .Activate(and_5_out),
    .Data_bit_0(input_output_register_1_output_bit_0), .Data_bit_1(input_output_register_1_output_bit_1),
    .Data_bit_2(input_output_register_1_output_bit_2), .Data_bit_3(input_output_register_1_output_bit_3));
  Nibble nibble_6 (
    .output_bit_0(nibble_6_output_bit_0), .output_bit_1(nibble_6_output_bit_1),
    .output_bit_2(nibble_6_output_bit_2), .output_bit_3(nibble_6_output_bit_3), .Activate(and_6_out),
    .Data_bit_0(input_output_register_1_output_bit_0), .Data_bit_1(input_output_register_1_output_bit_1),
    .Data_bit_2(input_output_register_1_output_bit_2), .Data_bit_3(input_output_register_1_output_bit_3));
  Nibble nibble_7 (
    .output_bit_0(nibble_7_output_bit_0), .output_bit_1(nibble_7_output_bit_1),
    .output_bit_2(nibble_7_output_bit_2), .output_bit_3(nibble_7_output_bit_3), .Activate(and_7_out),
    .Data_bit_0(input_output_register_1_output_bit_0), .Data_bit_1(input_output_register_1_output_bit_1),
    .Data_bit_2(input_output_register_1_output_bit_2), .Data_bit_3(input_output_register_1_output_bit_3));
  Nibble nibble_8 (
    .output_bit_0(nibble_8_output_bit_0), .output_bit_1(nibble_8_output_bit_1),
    .output_bit_2(nibble_8_output_bit_2), .output_bit_3(nibble_8_output_bit_3), .Activate(and_8_out),
    .Data_bit_0(input_output_register_1_output_bit_0), .Data_bit_1(input_output_register_1_output_bit_1),
    .Data_bit_2(input_output_register_1_output_bit_2), .Data_bit_3(input_output_register_1_output_bit_3));
  Input_output_register input_output_register_1 (
    .output_bit_0(input_output_register_1_output_bit_0), .output_bit_1(input_output_register_1_output_bit_1),
    .output_bit_2(input_output_register_1_output_bit_2), .output_bit_3(input_output_register_1_output_bit_3),
    .status_out(input_output_register_1_status_out), .Activate(Ram_Clock_out), .Data_bit_0(or_1_out),
    .Data_bit_1(or_2_out), .Data_bit_2(or_3_out), .Data_bit_3(or_4_out),
    .status_in(mode_register_1_output_mode_bit));
  and and_17 (o0, mode_register_1_output_mode_bit, input_output_register_1_status_out, input_output_register_1_output_bit_0);
  and and_18 (o1, mode_register_1_output_mode_bit, input_output_register_1_status_out, input_output_register_1_output_bit_1);
  and and_19 (and_19_out, ~address_register_1_output_bit_2, ~address_register_1_output_bit_1, ~address_register_1_output_bit_0);  // AND_Gate
  and and_20 (o2, mode_register_1_output_mode_bit, input_output_register_1_status_out, input_output_register_1_output_bit_2);
  and and_21 (and_21_out, ~address_register_1_output_bit_2, ~address_register_1_output_bit_1, address_register_1_output_bit_0);  // AND_Gate
  and and_22 (o3, mode_register_1_output_mode_bit, input_output_register_1_status_out, input_output_register_1_output_bit_3);
  and and_23 (and_23_out, ~address_register_1_output_bit_2, address_register_1_output_bit_1, ~address_register_1_output_bit_0);  // AND_Gate
  and and_24 (and_24_out, ~address_register_1_output_bit_2, address_register_1_output_bit_1, address_register_1_output_bit_0);  // AND_Gate
  and and_25 (and_25_out, address_register_1_output_bit_2, ~address_register_1_output_bit_1, ~address_register_1_output_bit_0);  // AND_Gate
  and and_26 (and_26_out, address_register_1_output_bit_2, ~address_register_1_output_bit_1, address_register_1_output_bit_0);  // AND_Gate
  and and_27 (and_27_out, address_register_1_output_bit_2, address_register_1_output_bit_1, ~address_register_1_output_bit_0);  // AND_Gate
  and and_28 (and_28_out, address_register_1_output_bit_2, address_register_1_output_bit_1, address_register_1_output_bit_0);
  and and_29 (and_29_out, nibble_1_output_bit_0, Ram_Clock_out, mode_register_1_output_mode_bit, and_19_out);
  and and_30 (and_30_out, nibble_1_output_bit_1, Ram_Clock_out, mode_register_1_output_mode_bit, and_19_out);
  and and_31 (and_31_out, nibble_2_output_bit_0, Ram_Clock_out, mode_register_1_output_mode_bit, and_21_out);
  and and_32 (and_32_out, nibble_2_output_bit_1, Ram_Clock_out, mode_register_1_output_mode_bit, and_21_out);
  and and_33 (and_33_out, nibble_3_output_bit_0, Ram_Clock_out, mode_register_1_output_mode_bit, and_23_out);
  and and_34 (and_34_out, nibble_3_output_bit_1, Ram_Clock_out, mode_register_1_output_mode_bit, and_23_out);
  and and_35 (and_35_out, nibble_4_output_bit_0, Ram_Clock_out, mode_register_1_output_mode_bit, and_24_out);
  and and_36 (and_36_out, nibble_4_output_bit_1, Ram_Clock_out, mode_register_1_output_mode_bit, and_24_out);
  and and_37 (and_37_out, nibble_5_output_bit_0, Ram_Clock_out, mode_register_1_output_mode_bit, and_25_out);
  and and_38 (and_38_out, nibble_5_output_bit_1, Ram_Clock_out, mode_register_1_output_mode_bit, and_25_out);
  and and_39 (and_39_out, nibble_6_output_bit_0, Ram_Clock_out, mode_register_1_output_mode_bit, and_26_out);
  and and_40 (and_40_out, nibble_6_output_bit_1, Ram_Clock_out, mode_register_1_output_mode_bit, and_26_out);
  and and_41 (and_41_out, nibble_7_output_bit_0, Ram_Clock_out, mode_register_1_output_mode_bit, and_27_out);
  and and_42 (and_42_out, nibble_7_output_bit_1, Ram_Clock_out, mode_register_1_output_mode_bit, and_27_out);
  and and_43 (and_43_out, nibble_8_output_bit_0, Ram_Clock_out, mode_register_1_output_mode_bit, and_28_out);
  and and_44 (and_44_out, nibble_8_output_bit_1, Ram_Clock_out, mode_register_1_output_mode_bit, and_28_out);
  and and_45 (and_45_out, nibble_1_output_bit_2, Ram_Clock_out, mode_register_1_output_mode_bit, and_19_out);
  and and_46 (and_46_out, nibble_2_output_bit_2, Ram_Clock_out, mode_register_1_output_mode_bit, and_21_out);
  and and_47 (and_47_out, nibble_3_output_bit_2, Ram_Clock_out, mode_register_1_output_mode_bit, and_23_out);
  and and_48 (and_48_out, nibble_4_output_bit_2, Ram_Clock_out, mode_register_1_output_mode_bit, and_24_out);
  and and_49 (and_49_out, nibble_5_output_bit_2, Ram_Clock_out, mode_register_1_output_mode_bit, and_25_out);
  and and_50 (and_50_out, nibble_6_output_bit_2, Ram_Clock_out, mode_register_1_output_mode_bit, and_26_out);
  and and_51 (and_51_out, nibble_7_output_bit_2, Ram_Clock_out, mode_register_1_output_mode_bit, and_27_out);
  and and_52 (and_52_out, nibble_8_output_bit_2, Ram_Clock_out, mode_register_1_output_mode_bit, and_28_out);
  and and_53 (and_53_out, nibble_1_output_bit_3, Ram_Clock_out, mode_register_1_output_mode_bit, and_19_out);
  and and_54 (and_54_out, nibble_2_output_bit_3, Ram_Clock_out, mode_register_1_output_mode_bit, and_21_out);
  and and_55 (and_55_out, nibble_3_output_bit_3, Ram_Clock_out, mode_register_1_output_mode_bit, and_23_out);
  and and_56 (and_56_out, nibble_4_output_bit_3, Ram_Clock_out, mode_register_1_output_mode_bit, and_24_out);
  and and_57 (and_57_out, nibble_5_output_bit_3, Ram_Clock_out, mode_register_1_output_mode_bit, and_25_out);
  and and_58 (and_58_out, nibble_6_output_bit_3, Ram_Clock_out, mode_register_1_output_mode_bit, and_26_out);
  and and_59 (and_59_out, nibble_7_output_bit_3, Ram_Clock_out, mode_register_1_output_mode_bit, and_27_out);
  and and_60 (and_60_out, nibble_8_output_bit_3, Ram_Clock_out, mode_register_1_output_mode_bit, and_28_out);
  or or_5 (or_5_out, or_6_out, and_53_out);
  or or_6 (or_6_out, or_7_out, and_54_out);
  or or_7 (or_7_out, or_8_out, and_55_out);
  or or_8 (or_8_out, or_9_out, and_56_out);
  or or_9 (or_9_out, or_10_out, and_57_out);
  or or_10 (or_10_out, or_11_out, and_58_out);
  or or_11 (or_11_out, and_60_out, and_59_out);
  or or_12 (or_12_out, or_13_out, and_45_out);
  or or_13 (or_13_out, or_14_out, and_46_out);
  or or_14 (or_14_out, or_15_out, and_47_out);
  or or_15 (or_15_out, or_16_out, and_48_out);
  or or_16 (or_16_out, or_17_out, and_49_out);
  or or_17 (or_17_out, or_18_out, and_50_out);
  or or_18 (or_18_out, and_52_out, and_51_out);
  or or_19 (or_19_out, or_20_out, and_30_out);
  or or_20 (or_20_out, or_21_out, and_32_out);
  or or_21 (or_21_out, or_22_out, and_34_out);
  or or_22 (or_22_out, or_23_out, and_36_out);
  or or_23 (or_23_out, or_24_out, and_38_out);
  or or_24 (or_24_out, or_25_out, and_40_out);
  or or_25 (or_25_out, and_44_out, and_42_out);
  or or_26 (or_26_out, or_27_out, and_29_out);
  or or_27 (or_27_out, or_28_out, and_31_out);
  or or_28 (or_28_out, or_29_out, and_33_out);
  or or_29 (or_29_out, or_30_out, and_35_out);
  or or_30 (or_30_out, or_31_out, and_37_out);
  or or_31 (or_31_out, or_32_out, and_39_out);
  or or_32 (or_32_out, and_43_out, and_41_out);

  // Notes on the sheet:
  //   3-bit address input pins
  //   Mode_Input_pin
  //   4-bit data input pins
  //   clock
  //   a0
  //   a1
  //   a2
  //   mode
  //   0
  //   1
  //   2
  //   3
  //   4
  //   5
  //   6
  //   7
  //   0
  //   1
  //   2
  //   3
  //   clock
  //   mode
  //   0
  //   0
  //   1
  //   1
  //   2
  //   2
  //   3
  //   3
  //   4
  //   4
  //   4-bit data output pins
  //   5
  //   5
  //   6
  //   6
  //   7
  //   7
  //   0ut_3
  //   0ut_2
  //   0ut_1
  //   0ut_0
endmodule

module Nibble (
  input  Data_bit_0,
  input  Data_bit_1,
  input  Data_bit_2,
  input  Data_bit_3,
  input  Activate,
  output output_bit_0,
  output output_bit_1,
  output output_bit_2,
  output output_bit_3
);

  wire and_1_out, and_2_out, and_3_out, and_4_out, and_5_out, and_6_out, and_7_out, and_8_out;

  and and_1 (and_1_out, Activate, ~Data_bit_0);  // AND_Gate
  and and_2 (and_2_out, Data_bit_0, Activate);
  and and_3 (and_3_out, Activate, ~Data_bit_1);  // AND_Gate
  and and_4 (and_4_out, Data_bit_1, Activate);
  and and_5 (and_5_out, Activate, ~Data_bit_2);  // AND_Gate
  and and_6 (and_6_out, Data_bit_2, Activate);
  and and_7 (and_7_out, Activate, ~Data_bit_3);  // AND_Gate
  and and_8 (and_8_out, Data_bit_3, Activate);
  flip_flop flip_flop_1 (.Q(output_bit_0), .Reset(and_1_out), .Set(and_2_out));  // open: not_Q
  flip_flop flip_flop_2 (.Q(output_bit_1), .Reset(and_3_out), .Set(and_4_out));  // open: not_Q
  flip_flop flip_flop_3 (.Q(output_bit_2), .Reset(and_5_out), .Set(and_6_out));  // open: not_Q
  flip_flop flip_flop_4 (.Q(output_bit_3), .Reset(and_7_out), .Set(and_8_out));  // open: not_Q
endmodule

module flip_flop (
  input  Reset,
  input  Set,
  output Q,
  output not_Q
);

  nor nor_1 (Q, Reset, not_Q);
  nor nor_2 (not_Q, Q, Set);
endmodule

module address_register (
  input  Data_bit_0,
  input  Data_bit_1,
  input  Data_bit_2,
  input  Activate,
  output s_bit_0,
  output s_bit_1,
  output s_bit_2,
  output output_bit_0,
  output output_bit_1,
  output output_bit_2
);

  wire and_1_out, and_2_out, and_3_out, and_4_out, and_5_out, and_6_out, and_7_out, and_8_out, and_9_out,
       and_10_out, and_11_out, and_12_out, not_1_out;

  not not_1 (not_1_out, Activate);
  and and_1 (and_1_out, not_1_out, ~Data_bit_0);  // AND_Gate
  and and_2 (and_2_out, Data_bit_0, not_1_out);
  and and_3 (and_3_out, not_1_out, ~Data_bit_1);  // AND_Gate
  and and_4 (and_4_out, Data_bit_1, not_1_out);
  and and_5 (and_5_out, not_1_out, ~Data_bit_2);  // AND_Gate
  and and_6 (and_6_out, Data_bit_2, not_1_out);
  flip_flop flip_flop_1 (.Q(output_bit_0), .Reset(and_1_out), .Set(and_2_out));  // open: not_Q
  flip_flop flip_flop_2 (.Q(output_bit_1), .Reset(and_3_out), .Set(and_4_out));  // open: not_Q
  flip_flop flip_flop_3 (.Q(output_bit_2), .Reset(and_5_out), .Set(and_6_out));  // open: not_Q
  and and_7 (and_7_out, Activate, ~output_bit_0);  // AND_Gate
  and and_8 (and_8_out, output_bit_0, Activate);
  and and_9 (and_9_out, Activate, ~output_bit_1);  // AND_Gate
  and and_10 (and_10_out, output_bit_1, Activate);
  and and_11 (and_11_out, Activate, ~output_bit_2);  // AND_Gate
  and and_12 (and_12_out, output_bit_2, Activate);
  flip_flop flip_flop_4 (.Q(s_bit_0), .Reset(and_7_out), .Set(and_8_out));  // open: not_Q
  flip_flop flip_flop_5 (.Q(s_bit_1), .Reset(and_9_out), .Set(and_10_out));  // open: not_Q
  flip_flop flip_flop_6 (.Q(s_bit_2), .Reset(and_11_out), .Set(and_12_out));  // open: not_Q

  // Notes on the sheet:
  //   store_bit_0
  //   store_bit_1
  //   store_bit_2
endmodule

module Input_output_register (
  input  Data_bit_0,
  input  Data_bit_1,
  input  Data_bit_2,
  input  Data_bit_3,
  input  status_in,
  input  Activate,
  output output_bit_0,
  output output_bit_1,
  output output_bit_2,
  output output_bit_3,
  output status_out
);

  wire and_1_out, and_2_out, and_3_out, and_4_out, and_5_out, and_6_out, and_7_out, and_8_out, and_9_out,
       and_10_out;

  and and_1 (and_1_out, Activate, ~Data_bit_0);  // AND_Gate
  and and_2 (and_2_out, Data_bit_0, Activate);
  and and_3 (and_3_out, Activate, ~Data_bit_1);  // AND_Gate
  and and_4 (and_4_out, Data_bit_1, Activate);
  and and_5 (and_5_out, Activate, ~Data_bit_2);  // AND_Gate
  and and_6 (and_6_out, Data_bit_2, Activate);
  and and_7 (and_7_out, Activate, ~Data_bit_3);  // AND_Gate
  and and_8 (and_8_out, Data_bit_3, Activate);
  and and_9 (and_9_out, Activate, ~status_in);  // AND_Gate
  and and_10 (and_10_out, status_in, Activate);
  flip_flop flip_flop_1 (.Q(output_bit_0), .Reset(and_1_out), .Set(and_2_out));  // open: not_Q
  flip_flop flip_flop_2 (.Q(output_bit_1), .Reset(and_3_out), .Set(and_4_out));  // open: not_Q
  flip_flop flip_flop_3 (.Q(output_bit_2), .Reset(and_5_out), .Set(and_6_out));  // open: not_Q
  flip_flop flip_flop_4 (.Q(output_bit_3), .Reset(and_7_out), .Set(and_8_out));  // open: not_Q
  flip_flop flip_flop_5 (.Q(status_out), .Reset(and_9_out), .Set(and_10_out));  // open: not_Q

  // Notes on the sheet:
  //   store_bit_0
  //   store_bit_1
  //   store_bit_2
  //   store_bit_3
endmodule

module mode_register (
  input  input_mode_bit,
  input  activate,
  output pre_mode_bit,
  output output_mode_bit
);

  wire and_1_out, and_2_out, and_3_out, and_4_out, not_1_out;

  not not_1 (not_1_out, activate);
  and and_1 (and_1_out, not_1_out, ~input_mode_bit);  // AND_Gate
  and and_2 (and_2_out, input_mode_bit, not_1_out);
  flip_flop flip_flop_1 (.Q(output_mode_bit), .Reset(and_1_out), .Set(and_2_out));  // open: not_Q
  and and_3 (and_3_out, activate, ~output_mode_bit);  // AND_Gate
  and and_4 (and_4_out, output_mode_bit, activate);
  flip_flop flip_flop_2 (.Q(pre_mode_bit), .Reset(and_3_out), .Set(and_4_out));  // open: not_Q

  // Notes on the sheet:
  //   store_bit_mode
endmodule
