// Logisim project a6Sol.circ as structural Verilog: 2 circuits, main circuit main
module main (
  input  in_1,
  input  in_2,
  input  in_3,
  input  in_4,
  input  in_5,
  input  in_6,
  input  in_7,
  input  in_8,
  input  in_9,
  output Zero,
  output Negative,
  output Overflow,
  output out_13,
  output out_14,
  output out_15,
  output out_16
);

  wire and_1_out, and_2_out, and_3_out, and_4_out, and_5_out, and_6_out, and_7_out, and_8_out, and_9_out,
       and_10_out, and_11_out, and_12_out, and_13_out, and_14_out, and_15_out, and_16_out, and_17_out,
       and_18_out, and_19_out, and_20_out, and_21_out, and_22_out, and_24_out, and_25_out, and_26_out,
       and_27_out, Clock, filladder_1_c, filladder_2_c, filladder_3_c, Neg_out, not_1_out, not_2_out,
       not_3_out, not_4_out, not_5_out, not_6_out, not_7_out, not_8_out, not_9_out, not_10_out, not_11_out,
       not_12_out, not_13_out, not_14_out, not_15_out, or_1_out, or_2_out, or_3_out, or_4_out, or_5_out,
       Pos_out, xor_2_out, xor_3_out, xor_4_out, xor_5_out;

  Clock clock_1 (.out(Clock));
  not not_1 (not_1_out, in_9);
  and and_1 (and_1_out, in_1, Clock);
  and and_2 (and_2_out, in_2, Clock);
  and and_3 (and_3_out, in_3, Clock);
  FillAdder filladder_1 (.A(or_1_out), .B(and_1_out), .Carry(filladder_2_c), .C(filladder_1_c), .Sum(Negative));
  and and_4 (and_4_out, in_4, Clock);
  FillAdder filladder_2 (.A(or_2_out), .B(and_2_out), .Carry(filladder_3_c), .C(filladder_2_c), .Sum(out_14));
  or or_1 (or_1_out, xor_2_out, and_6_out);
  FillAdder filladder_3 (.A(or_3_out), .B(and_3_out), .Carry(and_5_out), .C(filladder_3_c), .Sum(out_15));
  or or_2 (or_2_out, xor_3_out, and_8_out);
  or or_3 (or_3_out, xor_4_out, and_9_out);
  and and_5 (and_5_out, and_4_out, or_4_out);
  xor xor_1 (out_16, and_4_out, or_4_out);
  and and_6 (and_6_out, and_12_out, not_1_out);
  and and_7 (and_7_out, not_6_out, and_10_out);
  or or_4 (or_4_out, xor_5_out, and_14_out);
  not not_2 (not_2_out, out_16);
  not not_3 (not_3_out, out_15);
  not not_4 (not_4_out, out_14);
  not not_5 (not_5_out, Negative);
  and and_8 (and_8_out, and_13_out, not_1_out);
  and and_9 (and_9_out, and_17_out, not_1_out);
  xor xor_2 (xor_2_out, not_6_out, and_10_out);
  and and_10 (and_10_out, not_10_out, and_16_out);
  and and_11 (and_11_out, not_2_out, not_3_out, not_4_out, not_5_out);
  and and_12 (and_12_out, in_5, Clock);
  and and_13 (and_13_out, in_6, Clock);
  and and_14 (and_14_out, and_18_out, not_1_out);
  and and_15 (and_15_out, and_12_out, in_9);
  not not_6 (not_6_out, and_15_out);
  xor xor_3 (xor_3_out, not_10_out, and_16_out);
  and and_16 (and_16_out, not_11_out, and_22_out);
  not not_7 (not_7_out, or_1_out);
  not not_8 (not_8_out, and_1_out);
  not not_9 (not_9_out, or_1_out);
  and and_17 (and_17_out, in_7, Clock);
  and and_18 (and_18_out, in_8, Clock);
  and and_19 (and_19_out, and_13_out, in_9);
  and and_20 (and_20_out, and_17_out, in_9);
  and and_21 (and_21_out, and_18_out, in_9);
  not not_10 (not_10_out, and_19_out);
  not not_11 (not_11_out, and_20_out);
  not not_12 (not_12_out, and_21_out);
  xor xor_4 (xor_4_out, not_11_out, and_22_out);
  and and_22 (and_22_out, not_12_out, 1'b1);
  and Neg (Neg_out, or_1_out, and_1_out);
  and Pos (Pos_out, not_7_out, not_8_out);
  and and_23 (Zero, and_11_out, Clock);
  xor xor_5 (xor_5_out, not_12_out, 1'b1);
  and and_24 (and_24_out, Negative, Neg_out);
  and and_25 (and_25_out, Pos_out, Negative);
  and and_26 (and_26_out, not_13_out, not_9_out, filladder_1_c);
  not not_13 (not_13_out, in_9);
  not not_14 (not_14_out, filladder_1_c);
  and and_27 (and_27_out, and_24_out, not_14_out);
  or or_5 (or_5_out, and_26_out, and_25_out, and_27_out);
  not not_15 (not_15_out, Zero);
  and notZero (Overflow, or_5_out, not_15_out);

  assign out_13 = Negative;

  // Other names for the same wires on the sheet: CMD = in_9

  // Notes on the sheet:
  //   Add/Sub command
  //   0 add, 1 sub
  //   B Input
  //   L input
  //   A-out output
  //   A Input
  //   Adder
  //   R Input
  //   2's Complement
  //   Status output
  //   -8 + -8 is underflow (not supported)
endmodule

module FillAdder (
  input  A,
  input  B,
  input  Carry,
  output C,
  output Sum
);

  wire and_1_out, and_2_out, xor_1_out;

  and and_1 (and_1_out, A, B);
  xor xor_1 (xor_1_out, A, B);
  and and_2 (and_2_out, xor_1_out, Carry);
  or or_1 (C, and_1_out, and_2_out);
  xor xor_2 (Sum, xor_1_out, Carry);
endmodule
