// Logisim project mini6.circ as structural Verilog: 7 circuits, main circuit main
module main (
  input  L_3,
  input  L_2,
  input  L_1,
  input  L_0,
  input  R_3,
  input  R_2,
  input  R_1,
  input  R_0,
  input  Add_Sub_command,
  output negative_0,
  output zero_1,
  output overflow_2,
  output a_3,
  output a_2,
  output a_1,
  output a_0
);

  wire Adder_overflow, Adder_s_0, Adder_s_1, Adder_s_2, Adder_s_3, ALU_clock_out, and_1_out, buffer_1_out,
       buffer_2_out, buffer_3_out, buffer_4_out, buffer_5_out, buffer_6_out, buffer_7_out, buffer_8_out,
       buffer_9_out, buffer_10_out, buffer_11_out, buffer_12_out, buffer_13_out, buffer_14_out,
       buffer_15_out, buffer_16_out, buffer_17_out, buffer_18_out, buffer_19_out, buffer_20_out,
       buffer_21_out, buffer_22_out, buffer_23_out, buffer_24_out, buffer_25_out, buffer_26_out,
       buffer_27_out, buffer_28_out, buffer_29_out, buffer_30_out, buffer_31_out, buffer_32_out,
       buffer_33_out, buffer_34_out, buffer_35_out, buffer_36_out, buffer_37_out, buffer_38_out,
       buffer_39_out, buffer_40_out, buffer_41_out, buffer_42_out, buffer_43_out, buffer_44_out,
       buffer_45_out, buffer_46_out, buffer_47_out, buffer_48_out, buffer_49_out, buffer_50_out,
       buffer_51_out, buffer_52_out, buffer_53_out, buffer_54_out, buffer_55_out, buffer_56_out,
       buffer_57_out, buffer_58_out, buffer_59_out, buffer_60_out, buffer_61_out, buffer_62_out,
       buffer_63_out, buffer_64_out, buffer_65_out, buffer_66_out, buffer_67_out, buffer_68_out,
       buffer_69_out, buffer_70_out, buffer_71_out, buffer_72_out, buffer_73_out, buffer_74_out,
       buffer_75_out, buffer_76_out, buffer_77_out, buffer_78_out, buffer_79_out, buffer_80_out,
       buffer_81_out, buffer_82_out, buffer_83_out, buffer_84_out, buffer_85_out, buffer_86_out,
       complement_2_1_out_0, complement_2_1_out_1, complement_2_1_out_2, complement_2_1_out_3,
       Left_register_o_bit_0, Left_register_o_bit_1, Left_register_o_bit_2, Left_register_o_bit_3,
       Right_register_o_bit_0, Right_register_o_bit_1, Right_register_o_bit_2, Right_register_o_bit_3;

  Clock ALU_clock (.out(ALU_clock_out));
  buf buffer_1 (buffer_1_out, ALU_clock_out);
  buf buffer_2 (buffer_2_out, buffer_4_out);
  buf buffer_3 (buffer_3_out, buffer_1_out);
  buf buffer_4 (buffer_4_out, buffer_6_out);
  buf buffer_5 (buffer_5_out, buffer_3_out);
  buf buffer_6 (buffer_6_out, buffer_8_out);
  buf buffer_7 (buffer_7_out, buffer_5_out);
  buf buffer_8 (buffer_8_out, buffer_10_out);
  buf buffer_9 (buffer_9_out, buffer_7_out);
  buf buffer_10 (buffer_10_out, buffer_12_out);
  buf buffer_11 (buffer_11_out, buffer_9_out);
  buf buffer_12 (buffer_12_out, buffer_14_out);
  buf buffer_13 (buffer_13_out, buffer_11_out);
  buf buffer_14 (buffer_14_out, buffer_16_out);
  buf buffer_15 (buffer_15_out, buffer_13_out);
  buf buffer_16 (buffer_16_out, buffer_18_out);
  buf buffer_17 (buffer_17_out, buffer_15_out);
  buf buffer_18 (buffer_18_out, buffer_20_out);
  buf buffer_19 (buffer_19_out, buffer_17_out);
  buf buffer_20 (buffer_20_out, buffer_22_out);
  buf buffer_21 (buffer_21_out, buffer_19_out);
  buf buffer_22 (buffer_22_out, buffer_24_out);
  buf buffer_23 (buffer_23_out, buffer_21_out);
  buf buffer_24 (buffer_24_out, buffer_26_out);
  buf buffer_25 (buffer_25_out, buffer_23_out);
  buf buffer_26 (buffer_26_out, buffer_28_out);
  buf buffer_27 (buffer_27_out, buffer_25_out);
  buf buffer_28 (buffer_28_out, buffer_29_out);
  buf buffer_29 (buffer_29_out, buffer_27_out);
  buf buffer_30 (buffer_30_out, buffer_2_out);
  buf buffer_31 (buffer_31_out, buffer_30_out);
  buf buffer_32 (buffer_32_out, buffer_31_out);
  buf buffer_33 (buffer_33_out, buffer_32_out);
  buf buffer_34 (buffer_34_out, buffer_33_out);
  buf buffer_35 (buffer_35_out, buffer_34_out);
  buf buffer_36 (buffer_36_out, buffer_35_out);
  buf buffer_37 (buffer_37_out, buffer_36_out);
  buf buffer_38 (buffer_38_out, buffer_37_out);
  buf buffer_39 (buffer_39_out, buffer_38_out);
  buf buffer_40 (buffer_40_out, buffer_39_out);
  buf buffer_41 (buffer_41_out, buffer_40_out);
  buf buffer_42 (buffer_42_out, buffer_41_out);
  buf buffer_43 (buffer_43_out, buffer_42_out);
  L_R_register Left_register (
    .bit_0(L_0), .bit_1(L_1), .bit_2(L_2), .bit_3(L_3), .enable(ALU_clock_out),
    .o_bit_0(Left_register_o_bit_0), .o_bit_1(Left_register_o_bit_1), .o_bit_2(Left_register_o_bit_2),
    .o_bit_3(Left_register_o_bit_3));
  A_out_register a_out_register_1 (
    .bit_0(Adder_s_0), .bit_1(Adder_s_1), .bit_2(Adder_s_2), .bit_3(Adder_s_3), .Enable(buffer_43_out),
    .a_0(a_0), .a_1(a_1), .a_2(a_2), .a_3(a_3));
  L_R_register Right_register (
    .bit_0(R_0), .bit_1(R_1), .bit_2(R_2), .bit_3(R_3), .enable(ALU_clock_out),
    .o_bit_0(Right_register_o_bit_0), .o_bit_1(Right_register_o_bit_1), .o_bit_2(Right_register_o_bit_2),
    .o_bit_3(Right_register_o_bit_3));
  complement_2 complement_2_1 (
    .In3(Right_register_o_bit_3), .In2(Right_register_o_bit_2), .In1(Right_register_o_bit_1),
    .In0(Right_register_o_bit_0), .mode(Add_Sub_command), .out_3(complement_2_1_out_3),
    .out_2(complement_2_1_out_2), .out_1(complement_2_1_out_1), .out_0(complement_2_1_out_0));
  adder_4 Adder (
    .n1_3(Left_register_o_bit_3), .n1_2(Left_register_o_bit_2), .n1_1(Left_register_o_bit_1),
    .n1_0(Left_register_o_bit_0), .n2_3(complement_2_1_out_3), .n2_2(complement_2_1_out_2),
    .n2_1(complement_2_1_out_1), .n2_0(complement_2_1_out_0), .Enable(ALU_clock_out), .s_3(Adder_s_3),
    .s_2(Adder_s_2), .s_1(Adder_s_1), .s_0(Adder_s_0), .overflow(Adder_overflow));
  buf buffer_44 (buffer_44_out, ALU_clock_out);
  buf buffer_45 (buffer_45_out, buffer_44_out);
  buf buffer_46 (buffer_46_out, buffer_45_out);
  buf buffer_47 (buffer_47_out, buffer_48_out);
  buf buffer_48 (buffer_48_out, buffer_49_out);
  buf buffer_49 (buffer_49_out, buffer_55_out);
  buf buffer_50 (buffer_50_out, buffer_47_out);
  buf buffer_51 (buffer_51_out, buffer_46_out);
  buf buffer_52 (buffer_52_out, buffer_51_out);
  buf buffer_53 (buffer_53_out, buffer_52_out);
  buf buffer_54 (buffer_54_out, buffer_53_out);
  buf buffer_55 (buffer_55_out, buffer_56_out);
  buf buffer_56 (buffer_56_out, buffer_57_out);
  buf buffer_57 (buffer_57_out, buffer_58_out);
  buf buffer_58 (buffer_58_out, buffer_67_out);
  buf buffer_59 (buffer_59_out, buffer_50_out);
  buf buffer_60 (buffer_60_out, buffer_59_out);
  buf buffer_61 (buffer_61_out, buffer_60_out);
  buf buffer_62 (buffer_62_out, buffer_61_out);
  and and_1 (and_1_out, ~Adder_s_3, ~Adder_s_2, ~Adder_s_1, ~Adder_s_0);  // AND_Gate
  buf buffer_63 (buffer_63_out, buffer_54_out);
  buf buffer_64 (buffer_64_out, buffer_63_out);
  buf buffer_65 (buffer_65_out, buffer_64_out);
  buf buffer_66 (buffer_66_out, buffer_65_out);
  buf buffer_67 (buffer_67_out, buffer_68_out);
  buf buffer_68 (buffer_68_out, buffer_69_out);
  buf buffer_69 (buffer_69_out, buffer_70_out);
  buf buffer_70 (buffer_70_out, buffer_78_out);
  buf buffer_71 (buffer_71_out, buffer_62_out);
  buf buffer_72 (buffer_72_out, buffer_71_out);
  buf buffer_73 (buffer_73_out, buffer_72_out);
  buf buffer_74 (buffer_74_out, buffer_66_out);
  buf buffer_75 (buffer_75_out, buffer_74_out);
  buf buffer_76 (buffer_76_out, buffer_75_out);
  buf buffer_77 (buffer_77_out, buffer_76_out);
  buf buffer_78 (buffer_78_out, buffer_79_out);
  buf buffer_79 (buffer_79_out, buffer_80_out);
  buf buffer_80 (buffer_80_out, buffer_81_out);
  buf buffer_81 (buffer_81_out, buffer_85_out);
  buf buffer_82 (buffer_82_out, buffer_77_out);
  buf buffer_83 (buffer_83_out, buffer_82_out);
  buf buffer_84 (buffer_84_out, buffer_83_out);
  buf buffer_85 (buffer_85_out, buffer_86_out);
  buf buffer_86 (buffer_86_out, buffer_84_out);
  status_register status_register_1 (
    .bit_0(Adder_s_3), .bit_1(and_1_out), .bit_2(Adder_overflow), .Enable(buffer_73_out), .s_0(negative_0),
    .s_1(zero_1), .s_2(overflow_2));

  // Notes on the sheet:
  //   Jiahang Wang 261011319
  //   2's complement
endmodule

module adder_4 (
  input  n1_3,
  input  n1_2,
  input  n1_1,
  input  n1_0,
  input  n2_3,
  input  n2_2,
  input  n2_1,
  input  n2_0,
  input  Enable,
  output s_3,
  output s_2,
  output s_1,
  output s_0,
  output overflow
);

  wire and_1_out, and_2_out, and_3_out, and_4_out, and_5_out, controlled_buffer_1_out,
       controlled_buffer_2_out, controlled_buffer_3_out, controlled_buffer_4_out, controlled_buffer_5_out,
       controlled_buffer_6_out, controlled_buffer_7_out, controlled_buffer_8_out, half_adder_1_carry_out,
       half_adder_2_carry_out, half_adder_3_carry_out, or_1_out;

  assign controlled_buffer_1_out = Enable ? n1_0 : 1'bz;  // Controlled_Buffer controlled_buffer_1
  assign controlled_buffer_2_out = Enable ? n1_1 : 1'bz;  // Controlled_Buffer controlled_buffer_2
  assign controlled_buffer_3_out = Enable ? n1_2 : 1'bz;  // Controlled_Buffer controlled_buffer_3
  assign controlled_buffer_4_out = Enable ? n1_3 : 1'bz;  // Controlled_Buffer controlled_buffer_4
  assign controlled_buffer_5_out = Enable ? n2_0 : 1'bz;  // Controlled_Buffer controlled_buffer_5
  assign controlled_buffer_6_out = Enable ? n2_1 : 1'bz;  // Controlled_Buffer controlled_buffer_6
  assign controlled_buffer_7_out = Enable ? n2_2 : 1'bz;  // Controlled_Buffer controlled_buffer_7
  assign controlled_buffer_8_out = Enable ? n2_3 : 1'bz;  // Controlled_Buffer controlled_buffer_8
  and and_1 (and_1_out, ~controlled_buffer_4_out, ~controlled_buffer_8_out);  // AND_Gate
  and and_2 (and_2_out, controlled_buffer_4_out, controlled_buffer_8_out);
  half_adder half_adder_1 (
    .Bit_1(controlled_buffer_1_out), .Bit_2(controlled_buffer_5_out), .sum(s_0),
    .carry_out(half_adder_1_carry_out));  // open: carry_in
  half_adder half_adder_2 (
    .Bit_1(controlled_buffer_2_out), .Bit_2(controlled_buffer_6_out), .carry_in(half_adder_1_carry_out),
    .sum(s_1), .carry_out(half_adder_2_carry_out));
  half_adder half_adder_3 (
    .Bit_1(controlled_buffer_3_out), .Bit_2(controlled_buffer_7_out), .carry_in(half_adder_2_carry_out),
    .sum(s_2), .carry_out(half_adder_3_carry_out));
  half_adder half_adder_4 (
    .Bit_1(controlled_buffer_4_out), .Bit_2(controlled_buffer_8_out), .carry_in(half_adder_3_carry_out),
    .sum(s_3));  // open: carry_out
  and and_3 (and_3_out, and_1_out, s_3);
  and and_4 (and_4_out, and_2_out, ~s_3);  // AND_Gate
  and and_5 (and_5_out, s_3, ~s_2, ~s_1, ~s_0);  // AND_Gate
  or or_1 (or_1_out, and_5_out, and_4_out);
  or or_2 (overflow, and_3_out, or_1_out);
endmodule

module half_adder (
  input  Bit_1,
  input  Bit_2,
  input  carry_in,
  output sum,
  output carry_out
);

  wire and_1_out, and_2_out, and_3_out, and_4_out, and_5_out, and_6_out, and_7_out, and_8_out, not_1_out,
       not_2_out, not_3_out;

  not not_1 (not_1_out, Bit_1);
  not not_2 (not_2_out, Bit_2);
  not not_3 (not_3_out, carry_in);
  and and_1 (and_1_out, Bit_1, not_2_out, not_3_out);
  and and_2 (and_2_out, not_1_out, Bit_2, not_3_out);
  and and_3 (and_3_out, not_1_out, not_2_out, carry_in);
  and and_4 (and_4_out, Bit_1, Bit_2, carry_in);
  and and_5 (and_5_out, Bit_1, Bit_2, not_3_out);
  and and_6 (and_6_out, Bit_1, not_2_out, carry_in);
  and and_7 (and_7_out, not_1_out, Bit_2, carry_in);
  and and_8 (and_8_out, Bit_1, Bit_2, carry_in);
  or or_1 (sum, and_1_out, and_2_out, and_3_out, and_4_out);
  or or_2 (carry_out, and_5_out, and_6_out, and_7_out, and_8_out);
endmodule

module complement_2 (
  input  In3,
  input  In2,
  input  In1,
  input  In0,
  input  mode,
  output out_3,
  output out_2,
  output out_1,
  output out_0
);

  wire adder_4_1_s_0, adder_4_1_s_1, adder_4_1_s_2, adder_4_1_s_3, and_1_out, and_2_out, and_3_out,
       and_4_out, and_5_out, and_6_out, and_7_out, and_8_out, not_1_out, not_2_out, not_3_out, not_4_out;

  and and_1 (and_1_out, In3, ~mode);  // AND_Gate
  or or_1 (out_3, and_1_out, adder_4_1_s_3);
  and and_2 (and_2_out, In2, ~mode);  // AND_Gate
  or or_2 (out_2, and_2_out, adder_4_1_s_2);
  and and_3 (and_3_out, In1, ~mode);  // AND_Gate
  or or_3 (out_1, and_3_out, adder_4_1_s_1);
  and and_4 (and_4_out, In0, ~mode);  // AND_Gate
  or or_4 (out_0, and_4_out, adder_4_1_s_0);
  and and_5 (and_5_out, In0, mode);
  not not_1 (not_1_out, and_5_out);
  and and_6 (and_6_out, In1, mode);
  not not_2 (not_2_out, and_6_out);
  and and_7 (and_7_out, In3, mode);
  and and_8 (and_8_out, In2, mode);
  not not_3 (not_3_out, and_7_out);
  not not_4 (not_4_out, and_8_out);
  adder_4 adder_4_1 (
    .n1_3(not_3_out), .n1_2(not_4_out), .n1_1(not_2_out), .n1_0(not_1_out), .n2_0(mode), .Enable(mode),
    .s_3(adder_4_1_s_3), .s_2(adder_4_1_s_2), .s_1(adder_4_1_s_1), .s_0(adder_4_1_s_0));  // open: n2_3, n2_2, n2_1, overflow
endmodule

module L_R_register (
  input  bit_0,
  input  bit_1,
  input  bit_2,
  input  bit_3,
  input  enable,
  output o_bit_0,
  output o_bit_1,
  output o_bit_2,
  output o_bit_3
);

  assign o_bit_0 = enable ? bit_0 : 1'bz;  // Controlled_Buffer controlled_buffer_1
  assign o_bit_1 = enable ? bit_1 : 1'bz;  // Controlled_Buffer controlled_buffer_2
  assign o_bit_2 = enable ? bit_2 : 1'bz;  // Controlled_Buffer controlled_buffer_3
  assign o_bit_3 = enable ? bit_3 : 1'bz;  // Controlled_Buffer controlled_buffer_4
  D_Flip_Flop d_ff_1 (.D(bit_0), .clk(enable));  // open: Q, Qn, preset, reset
  D_Flip_Flop d_ff_2 (.D(bit_1), .clk(enable));  // open: Q, Qn, preset, reset
  D_Flip_Flop d_ff_3 (.D(bit_2), .clk(enable));  // open: Q, Qn, preset, reset
  D_Flip_Flop d_ff_4 (.D(bit_3), .clk(enable));  // open: Q, Qn, preset, reset
endmodule

module status_register (
  input  bit_0,
  input  bit_1,
  input  bit_2,
  input  Enable,
  output s_0,
  output s_1,
  output s_2
);

  D_Flip_Flop d_ff_1 (.D(bit_0), .clk(Enable), .Q(s_0));  // open: Qn, preset, reset
  D_Flip_Flop d_ff_2 (.D(bit_1), .clk(Enable), .Q(s_1));  // open: Qn, preset, reset
  D_Flip_Flop d_ff_3 (.D(bit_2), .clk(Enable), .Q(s_2));  // open: Qn, preset, reset
endmodule

module A_out_register (
  input  bit_0,
  input  bit_1,
  input  bit_2,
  input  bit_3,
  input  Enable,
  output a_0,
  output a_1,
  output a_2,
  output a_3
);

  D_Flip_Flop d_ff_1 (.D(bit_0), .clk(Enable), .Q(a_0));  // open: Qn, preset, reset
  D_Flip_Flop d_ff_2 (.D(bit_1), .clk(Enable), .Q(a_1));  // open: Qn, preset, reset
  D_Flip_Flop d_ff_3 (.D(bit_2), .clk(Enable), .Q(a_2));  // open: Qn, preset, reset
  D_Flip_Flop d_ff_4 (.D(bit_3), .clk(Enable), .Q(a_3));  // open: Qn, preset, reset
endmodule
